// Logisim project 4-XOR.circ as structural Verilog: 6 circuits, main circuit main
module main (
  input  in_1,
  input  in_2,
  input  in_3,
  input  in_4,
  output out_5,
  output out_6,
  output out_7,
  output out_8
);

  wire and_1_out, and_2_out, and_3_out, and_4_out, and_5_out, and_6_out, and_7_out, and_8_out, and_9_out,
       and_10_out, and_11_out, and_12_out, and_13_out, and_14_out, and_15_out, and_16_out, and_17_out,
       and_18_out, and_19_out, and_20_out, and_21_out, and_22_out, and_23_out, and_24_out, and_25_out,
       and_26_out, and_27_out, and_28_out, nand_1_out, nand_2_out, nand_3_out, nand_4_out, nand_5_out,
       nand_6_out, nand_7_out, nand_8_out, nand_9_out, nand_10_out, nand_11_out, nand_12_out, nand_13_out,
       nand_14_out, nand_15_out, nand_16_out, not_1_out, not_2_out, not_3_out, not_4_out, not_5_out,
       not_6_out, not_7_out, not_8_out, not_9_out, not_10_out, not_11_out, not_12_out, not_13_out,
       not_14_out, not_15_out, not_16_out, not_17_out, not_18_out, not_19_out, not_20_out, not_21_out,
       not_22_out, not_23_out, not_24_out, not_25_out, not_26_out, not_27_out, not_28_out;

  and and_1 (and_1_out, and_3_out, not_4_out);
  and and_2 (and_2_out, and_4_out, not_3_out);
  and and_3 (and_3_out, and_5_out, not_8_out);
  and and_4 (and_4_out, and_6_out, not_7_out);
  and and_5 (and_5_out, in_1, not_12_out);
  and and_6 (and_6_out, in_2, not_11_out);
  and and_7 (and_7_out, and_10_out, not_1_out);
  and and_8 (and_8_out, and_9_out, not_2_out);
  not not_1 (not_1_out, and_20_out);
  not not_2 (not_2_out, and_19_out);
  not not_3 (not_3_out, and_18_out);
  not not_4 (not_4_out, and_17_out);
  and and_9 (and_9_out, and_11_out, not_6_out);
  and and_10 (and_10_out, and_12_out, not_5_out);
  not not_5 (not_5_out, and_24_out);
  not not_6 (not_6_out, and_23_out);
  not not_7 (not_7_out, and_22_out);
  not not_8 (not_8_out, and_21_out);
  and and_11 (and_11_out, in_3, not_10_out);
  and and_12 (and_12_out, in_4, not_9_out);
  not not_9 (not_9_out, and_28_out);
  not not_10 (not_10_out, and_27_out);
  not not_11 (not_11_out, and_26_out);
  not not_12 (not_12_out, and_25_out);
  and and_13 (and_13_out, and_1_out, nand_1_out);
  nand nand_1 (nand_1_out, out_5, not_13_out);
  not not_13 (not_13_out, and_13_out);
  and and_14 (and_14_out, and_2_out, nand_2_out);
  nand nand_2 (nand_2_out, out_5, not_14_out);
  not not_14 (not_14_out, and_14_out);
  and and_15 (and_15_out, and_8_out, nand_3_out);
  nand nand_3 (nand_3_out, out_5, not_15_out);
  not not_15 (not_15_out, and_15_out);
  and and_16 (and_16_out, and_7_out, nand_4_out);
  nand nand_4 (nand_4_out, out_5, not_16_out);
  not not_16 (not_16_out, and_16_out);
  and and_17 (and_17_out, and_3_out, nand_5_out);
  nand nand_5 (nand_5_out, out_6, not_17_out);
  not not_17 (not_17_out, and_17_out);
  and and_18 (and_18_out, and_4_out, nand_6_out);
  nand nand_6 (nand_6_out, out_6, not_18_out);
  not not_18 (not_18_out, and_18_out);
  and and_19 (and_19_out, and_9_out, nand_7_out);
  nand nand_7 (nand_7_out, out_6, not_19_out);
  not not_19 (not_19_out, and_19_out);
  and and_20 (and_20_out, and_10_out, nand_8_out);
  nand nand_8 (nand_8_out, out_6, not_20_out);
  not not_20 (not_20_out, and_20_out);
  and and_21 (and_21_out, and_5_out, nand_9_out);
  nand nand_9 (nand_9_out, out_7, not_21_out);
  not not_21 (not_21_out, and_21_out);
  and and_22 (and_22_out, and_6_out, nand_10_out);
  nand nand_10 (nand_10_out, out_7, not_22_out);
  not not_22 (not_22_out, and_22_out);
  and and_23 (and_23_out, and_11_out, nand_11_out);
  nand nand_11 (nand_11_out, out_7, not_23_out);
  not not_23 (not_23_out, and_23_out);
  and and_24 (and_24_out, and_12_out, nand_12_out);
  nand nand_12 (nand_12_out, out_7, not_24_out);
  not not_24 (not_24_out, and_24_out);
  and and_25 (and_25_out, in_1, nand_13_out);
  nand nand_13 (nand_13_out, out_8, not_25_out);
  not not_25 (not_25_out, and_25_out);
  and and_26 (and_26_out, in_2, nand_14_out);
  nand nand_14 (nand_14_out, out_8, not_26_out);
  not not_26 (not_26_out, and_26_out);
  and and_27 (and_27_out, in_3, nand_15_out);
  nand nand_15 (nand_15_out, out_8, not_27_out);
  not not_27 (not_27_out, and_27_out);
  and and_28 (and_28_out, in_4, nand_16_out);
  nand nand_16 (nand_16_out, out_8, not_28_out);
  not not_28 (not_28_out, and_28_out);
  or or_1 (out_5, and_13_out, and_14_out, and_15_out, and_16_out);
  or or_2 (out_6, and_17_out, and_18_out, and_19_out, and_20_out);
  or or_3 (out_7, and_21_out, and_22_out, and_23_out, and_24_out);
  or or_4 (out_8, and_25_out, and_26_out, and_27_out, and_28_out);
endmodule

module Switch (
  input  in_1,
  input  in_2,
  output out_3
);

  and and_1 (out_3, in_1, in_2);
endmodule

module DELAY (
  input  in_1,
  input  in_2,
  input  in_3,
  input  in_4,
  input  [3:0] in_5,
  input  [7:0] in_6,
  input  [3:0] in_7,
  input  [3:0] in_8,
  input  in_9,
  input  in_10,
  input  in_11,
  input  [3:0] in_12,
  input  in_13,
  input  in_14,
  input  in_15,
  input  in_16,
  input  in_17,
  input  in_18,
  input  in_19,
  input  in_20,
  input  in_21,
  input  in_22,
  input  in_23,
  input  in_24,
  input  in_25,
  input  in_26,
  input  in_27,
  input  in_28,
  input  in_29,
  input  in_30,
  input  in_31,
  input  in_32,
  input  in_33,
  input  [6:0] in_34,
  input  [1:0] in_35,
  input  [6:0] in_36,
  input  [6:0] in_37,
  input  in_38,
  input  [6:0] in_39,
  input  in_40,
  input  [6:0] in_41,
  input  [3:0] in_42,
  input  in_43,
  input  in_44,
  input  in_45,
  output out_46,
  output out_47,
  output [3:0] out_48,
  output out_49,
  output [4:0] out_50,
  output out_51,
  output out_52,
  output [3:0] out_53,
  output out_54,
  output [1:0] out_55,
  output [3:0] out_56,
  output [3:0] out_57,
  output [3:0] out_58,
  output [3:0] out_59,
  output [3:0] out_60,
  output [3:0] out_61
);

  wire clock_1_out, clock_2_out, shift_register_1_out, shift_register_1_q0, shift_register_1_q1,
       shift_register_1_q2, shift_register_1_q3, shift_register_1_q4, shift_register_1_q5,
       shift_register_1_q6, shift_register_1_q7;
  wire [4:0] joystick_1_x, joystick_1_y;
  wire [6:0] keyboard_1_data;
  wire [7:0] random_1_out;

  Button button_1 ();  // open: out
  Random random_1 (.clk(clock_1_out), .out(random_1_out));  // open: next, clr
  // Odd_Parity odd_parity_1 is placed but not wired
  Shifter shifter_1 ();  // open: in, dist, out
  ROM #(.addrWidth(4), .dataWidth(4)) rom_1 (.addr(in_5), .data(out_48));  // open: sel
  Comparator #(.width(4)) comparator_1 (.a(in_7), .b(in_8), .gt(out_49), .eq(out_51), .lt(out_52));
  Register #(.width(1)) register_1 ();  // open: D, en, Q, clk, clr
  Shift_Register shift_register_1 (
    .shift(in_27), .in(in_28), .clk(clock_1_out), .out(shift_register_1_out), .load(in_14), .clr(in_30),
    .d0(in_15), .q0(shift_register_1_q0), .d1(in_16), .q1(shift_register_1_q1), .d2(in_17),
    .q2(shift_register_1_q2), .d3(in_18), .q3(shift_register_1_q3), .d4(in_19), .q4(shift_register_1_q4),
    .d5(in_20), .q5(shift_register_1_q5), .d6(in_21), .q6(shift_register_1_q6), .d7(in_22),
    .q7(shift_register_1_q7));
  Clock clock_1 (.out(clock_1_out));
  DotMatrix dotmatrix_1 (.col0(in_34), .col1(in_36), .col2(in_37), .col3(in_39), .col4(in_41));
  Clock clock_2 (.out(clock_2_out));
  Transistor transistor_1 (.in(in_3), .out(out_46), .gate(in_1));
  Keyboard keyboard_1 (.clk(clock_2_out), .re(in_23), .clr(in_24), .data(keyboard_1_data));  // open: avail
  assign out_55 = ~in_35;  // NOT_Gate not_1, 2 bits wide
  assign out_60 = ~in_42;  // NOT_Gate not_2, 4 bits wide
  RAM #(.dataWidth(5)) ram_1 (.addr(in_6), .data(out_50), .sel(in_9), .clk(in_13), .ld(in_10), .clr(in_11));
  // AND_Gate and_1 is placed but not wired
  Transistor #(.\type ("n")) transistor_2 (.in(in_4), .out(out_47), .gate(in_2));
  TTY tty_1 (.data(keyboard_1_data), .clk(clock_2_out), .we(in_25), .clr(in_26));
  DotMatrix #(.matrixrows(5)) dotmatrix_2 (.col0(joystick_1_x), .col1(joystick_1_y));  // open: col2, col3, col4
  Joystick #(.bits(5)) joystick_1 (.x(joystick_1_x), .y(joystick_1_y));
  assign out_56 = {{3{1'b0}}, in_38};  // Bit_Extender bit_extender_1
  assign out_58 = {{3{in_40}}, in_40};  // Bit_Extender bit_extender_2
  assign out_59 = {{3{1'b0}}, in_43};  // Bit_Extender bit_extender_3
  assign out_61 = {{3{1'b0}}, in_44};  // Bit_Extender bit_extender_4
  assign out_57 = out_56 | out_58 | out_59 | out_61;  // OR_Gate or_1, 4 bits wide

  assign out_53 = {in_33, in_32, in_31, in_29};

  // Notes on the sheet:
  //   contents of rom_1 (hex, n*v repeats v):
  //   0 0 0 1
endmodule

module game (
);

  wire decode_2_out_5, decode_2_out_6, decode_2_out_7, decode_2_out_8, decode_2_out_9, decode_2_out_10,
       decode_2_out_11, decode_2_out_12, decode_2_out_13, decode_2_out_14, decode_2_out_15, decode_2_out_16,
       decode_2_out_17, decode_2_out_18, decode_2_out_19;
  wire [3:0] joystick_1_x, joystick_1_y;
  wire [14:0] and_1_out, and_2_out, and_3_out, and_4_out, and_5_out, and_6_out, and_7_out, and_8_out,
       and_9_out, and_10_out, and_11_out, and_12_out, and_13_out, and_14_out, and_15_out, decode_1_out_19,
       extend_1_out_8, extend_1_out_9, extend_1_out_10, extend_1_out_11, extend_1_out_12, extend_1_out_13,
       extend_1_out_14, extend_2_out_8, extend_2_out_9, extend_2_out_10, extend_2_out_11, extend_2_out_12,
       extend_2_out_13, extend_2_out_14, extend_3_out_8;

  Joystick joystick_1 (.x(joystick_1_x), .y(joystick_1_y));
  decode decode_1 (
    .in_1(joystick_1_y[0]), .in_2(joystick_1_y[1]), .in_3(joystick_1_y[2]), .in_4(joystick_1_y[3]),
    .out_5(decode_1_out_19[14]), .out_6(decode_1_out_19[13]), .out_7(decode_1_out_19[12]),
    .out_8(decode_1_out_19[11]), .out_9(decode_1_out_19[10]), .out_10(decode_1_out_19[9]),
    .out_11(decode_1_out_19[8]), .out_12(decode_1_out_19[7]), .out_13(decode_1_out_19[6]),
    .out_14(decode_1_out_19[5]), .out_15(decode_1_out_19[4]), .out_16(decode_1_out_19[3]),
    .out_17(decode_1_out_19[2]), .out_18(decode_1_out_19[1]), .out_19(decode_1_out_19[0]));
  extend extend_1 (
    .in_1(decode_2_out_5), .in_2(decode_2_out_6), .in_3(decode_2_out_7), .in_4(decode_2_out_8),
    .in_5(decode_2_out_9), .in_6(decode_2_out_10), .in_7(decode_2_out_11), .out_8(extend_1_out_8),
    .out_9(extend_1_out_9), .out_10(extend_1_out_10), .out_11(extend_1_out_11), .out_12(extend_1_out_12),
    .out_13(extend_1_out_13), .out_14(extend_1_out_14));
  decode decode_2 (
    .in_1(joystick_1_x[0]), .in_2(joystick_1_x[1]), .in_3(joystick_1_x[2]), .in_4(joystick_1_x[3]),
    .out_5(decode_2_out_5), .out_6(decode_2_out_6), .out_7(decode_2_out_7), .out_8(decode_2_out_8),
    .out_9(decode_2_out_9), .out_10(decode_2_out_10), .out_11(decode_2_out_11), .out_12(decode_2_out_12),
    .out_13(decode_2_out_13), .out_14(decode_2_out_14), .out_15(decode_2_out_15), .out_16(decode_2_out_16),
    .out_17(decode_2_out_17), .out_18(decode_2_out_18), .out_19(decode_2_out_19));
  extend extend_2 (
    .in_1(decode_2_out_12), .in_2(decode_2_out_13), .in_3(decode_2_out_14), .in_4(decode_2_out_15),
    .in_5(decode_2_out_16), .in_6(decode_2_out_17), .in_7(decode_2_out_18), .out_8(extend_2_out_8),
    .out_9(extend_2_out_9), .out_10(extend_2_out_10), .out_11(extend_2_out_11), .out_12(extend_2_out_12),
    .out_13(extend_2_out_13), .out_14(extend_2_out_14));
  extend extend_3 (
    .in_1(decode_2_out_19), .out_8(extend_3_out_8));  // open: in_2, in_3, in_4, in_5, in_6, in_7, out_9, out_10, out_11, out_12, out_13, out_14
  assign and_1_out = decode_1_out_19 & extend_1_out_8;  // AND_Gate and_1, 15 bits wide
  assign and_2_out = decode_1_out_19 & extend_1_out_9;  // AND_Gate and_2, 15 bits wide
  DotMatrix #(.matrixcols(15), .matrixrows(15)) dotmatrix_1 (
    .col0(and_1_out), .col1(and_2_out), .col2(and_4_out), .col3(and_3_out), .col4(and_5_out),
    .col5(and_6_out), .col6(and_7_out), .col7(and_9_out), .col8(and_10_out), .col9(and_8_out),
    .col10(and_11_out), .col11(and_12_out), .col12(and_13_out), .col13(and_15_out), .col14(and_14_out));
  assign and_3_out = decode_1_out_19 & extend_1_out_11;  // AND_Gate and_3, 15 bits wide
  assign and_4_out = decode_1_out_19 & extend_1_out_10;  // AND_Gate and_4, 15 bits wide
  assign and_5_out = decode_1_out_19 & extend_1_out_12;  // AND_Gate and_5, 15 bits wide
  assign and_6_out = decode_1_out_19 & extend_1_out_13;  // AND_Gate and_6, 15 bits wide
  assign and_7_out = decode_1_out_19 & extend_1_out_14;  // AND_Gate and_7, 15 bits wide
  assign and_8_out = decode_1_out_19 & extend_2_out_10;  // AND_Gate and_8, 15 bits wide
  assign and_9_out = decode_1_out_19 & extend_2_out_8;  // AND_Gate and_9, 15 bits wide
  assign and_10_out = decode_1_out_19 & extend_2_out_9;  // AND_Gate and_10, 15 bits wide
  assign and_11_out = decode_1_out_19 & extend_2_out_11;  // AND_Gate and_11, 15 bits wide
  assign and_12_out = decode_1_out_19 & extend_2_out_12;  // AND_Gate and_12, 15 bits wide
  assign and_13_out = decode_1_out_19 & extend_2_out_13;  // AND_Gate and_13, 15 bits wide
  assign and_14_out = decode_1_out_19 & extend_3_out_8;  // AND_Gate and_14, 15 bits wide
  assign and_15_out = decode_1_out_19 & extend_2_out_14;  // AND_Gate and_15, 15 bits wide
endmodule

module decode (
  input  in_1,
  input  in_2,
  input  in_3,
  input  in_4,
  output out_5,
  output out_6,
  output out_7,
  output out_8,
  output out_9,
  output out_10,
  output out_11,
  output out_12,
  output out_13,
  output out_14,
  output out_15,
  output out_16,
  output out_17,
  output out_18,
  output out_19
);

  and and_1 (out_5, ~in_4, ~in_3, ~in_2, in_1);  // AND_Gate
  and and_2 (out_7, ~in_4, ~in_3, in_2, in_1);  // AND_Gate
  and and_3 (out_6, ~in_4, ~in_3, in_2, ~in_1);  // AND_Gate
  and and_4 (out_8, ~in_4, in_3, ~in_2, ~in_1);  // AND_Gate
  and and_5 (out_9, ~in_4, in_3, ~in_2, in_1);  // AND_Gate
  and and_6 (out_10, ~in_4, in_3, in_2, ~in_1);  // AND_Gate
  and and_7 (out_11, ~in_4, in_3, in_2, in_1);  // AND_Gate
  and and_8 (out_12, in_4, ~in_3, ~in_2, ~in_1);  // AND_Gate
  and and_9 (out_13, in_4, ~in_3, ~in_2, in_1);  // AND_Gate
  and and_10 (out_15, in_4, ~in_3, in_2, in_1);  // AND_Gate
  and and_11 (out_14, in_4, ~in_3, in_2, ~in_1);  // AND_Gate
  and and_12 (out_16, in_4, in_3, ~in_2, ~in_1);  // AND_Gate
  and and_13 (out_17, in_4, in_3, ~in_2, in_1);  // AND_Gate
  and and_14 (out_19, in_4, in_3, in_2, in_1);
  and and_15 (out_18, in_4, in_3, in_2, ~in_1);  // AND_Gate
endmodule

module extend (
  input  in_1,
  input  in_2,
  input  in_3,
  input  in_4,
  input  in_5,
  input  in_6,
  input  in_7,
  output [14:0] out_8,
  output [14:0] out_9,
  output [14:0] out_10,
  output [14:0] out_11,
  output [14:0] out_12,
  output [14:0] out_13,
  output [14:0] out_14
);

  assign out_8 = {{14{in_1}}, in_1};  // Bit_Extender bit_extender_1
  assign out_9 = {{14{in_2}}, in_2};  // Bit_Extender bit_extender_2
  assign out_10 = {{14{in_3}}, in_3};  // Bit_Extender bit_extender_3
  assign out_11 = {{14{in_4}}, in_4};  // Bit_Extender bit_extender_4
  assign out_12 = {{14{in_5}}, in_5};  // Bit_Extender bit_extender_5
  assign out_13 = {{14{in_6}}, in_6};  // Bit_Extender bit_extender_6
  assign out_14 = {{14{in_7}}, in_7};  // Bit_Extender bit_extender_7
endmodule
