// Logisim project BCD-Adder.circ as structural Verilog: 8 circuits, main circuit main
module main (
  input  in_1,
  input  in_2,
  input  in_3,
  input  in_4,
  input  in_5,
  input  in_6,
  input  in_7,
  input  in_8,
  input  in_9,
  input  in_10,
  input  in_11,
  input  in_12,
  input  in_13,
  input  in_14,
  input  in_15,
  input  in_16,
  input  in_17,
  input  in_18,
  input  in_19,
  input  in_20,
  input  in_21,
  input  in_22,
  input  in_23,
  input  in_24,
  input  in_25,
  input  in_26,
  input  in_27,
  input  in_28,
  input  in_29,
  input  in_30,
  input  in_31,
  input  in_32,
  input  in_33,
  input  in_34,
  input  in_35,
  input  in_36,
  input  in_37,
  input  in_38,
  input  in_39,
  input  in_40
);

  wire bcd_adder_1_out_11, bcd_adder_1_out_12, bcd_adder_1_out_13, bcd_adder_1_out_14, bcd_adder_2_c_out,
       bcd_adder_2_out_11, bcd_adder_2_out_12, bcd_adder_2_out_13, bcd_adder_2_out_14, bcd_adder_3_c_out,
       bcd_adder_3_out_11, bcd_adder_3_out_12, bcd_adder_3_out_13, bcd_adder_3_out_14, bcd_adder_4_c_out,
       bcd_adder_4_out_11, bcd_adder_4_out_12, bcd_adder_4_out_13, bcd_adder_4_out_14, bcd_adder_5_c_out,
       bcd_adder_5_out_11, bcd_adder_5_out_12, bcd_adder_5_out_13, bcd_adder_5_out_14, bcd_adder_6_c_out,
       bcd_adder_6_out_11, bcd_adder_6_out_12, bcd_adder_6_out_13, bcd_adder_6_out_14, bin_to_dec_1_out_5,
       bin_to_dec_1_out_6, bin_to_dec_1_out_7, bin_to_dec_1_out_8, bin_to_dec_1_out_9, bin_to_dec_1_out_10,
       bin_to_dec_1_out_11, bin_to_dec_2_out_5, bin_to_dec_2_out_6, bin_to_dec_2_out_7, bin_to_dec_2_out_8,
       bin_to_dec_2_out_9, bin_to_dec_2_out_10, bin_to_dec_2_out_11, bin_to_dec_3_out_5, bin_to_dec_3_out_6,
       bin_to_dec_3_out_7, bin_to_dec_3_out_8, bin_to_dec_3_out_9, bin_to_dec_3_out_10, bin_to_dec_3_out_11,
       bin_to_dec_4_out_5, bin_to_dec_4_out_6, bin_to_dec_4_out_7, bin_to_dec_4_out_8, bin_to_dec_4_out_9,
       bin_to_dec_4_out_10, bin_to_dec_4_out_11, bin_to_dec_5_out_5, bin_to_dec_5_out_6, bin_to_dec_5_out_7,
       bin_to_dec_5_out_8, bin_to_dec_5_out_9, bin_to_dec_5_out_10, bin_to_dec_5_out_11, bin_to_dec_6_out_5,
       bin_to_dec_6_out_6, bin_to_dec_6_out_7, bin_to_dec_6_out_8, bin_to_dec_6_out_9, bin_to_dec_6_out_10,
       bin_to_dec_6_out_11;

  BIN_TO_DEC bin_to_dec_1 (
    .in_1(bcd_adder_1_out_11), .in_2(bcd_adder_1_out_12), .in_3(bcd_adder_1_out_13),
    .in_4(bcd_adder_1_out_14), .out_5(bin_to_dec_1_out_5), .out_6(bin_to_dec_1_out_6),
    .out_7(bin_to_dec_1_out_7), .out_8(bin_to_dec_1_out_8), .out_9(bin_to_dec_1_out_9),
    .out_10(bin_to_dec_1_out_10), .out_11(bin_to_dec_1_out_11));
  _7_Segment_Display u_7_segment_display_1 (
    .g(bin_to_dec_1_out_8), .f(bin_to_dec_1_out_9), .a(bin_to_dec_1_out_10), .b(bin_to_dec_1_out_11),
    .e(bin_to_dec_1_out_5), .d(bin_to_dec_1_out_6), .c(bin_to_dec_1_out_7));  // open: dp
  BCD_ADDER bcd_adder_1 (
    .in_1(1'b0), .in_2(1'b0), .in_3(1'b0), .in_4(1'b0), .in_5(1'b0), .in_6(1'b0), .in_7(1'b0), .in_8(1'b0),
    .out_11(bcd_adder_1_out_11), .out_12(bcd_adder_1_out_12), .out_13(bcd_adder_1_out_13),
    .out_14(bcd_adder_1_out_14), .C_in(bcd_adder_2_c_out));  // open: C_out
  BIN_TO_DEC bin_to_dec_2 (
    .in_1(bcd_adder_2_out_11), .in_2(bcd_adder_2_out_12), .in_3(bcd_adder_2_out_13),
    .in_4(bcd_adder_2_out_14), .out_5(bin_to_dec_2_out_5), .out_6(bin_to_dec_2_out_6),
    .out_7(bin_to_dec_2_out_7), .out_8(bin_to_dec_2_out_8), .out_9(bin_to_dec_2_out_9),
    .out_10(bin_to_dec_2_out_10), .out_11(bin_to_dec_2_out_11));
  _7_Segment_Display u_7_segment_display_2 (
    .g(bin_to_dec_2_out_8), .f(bin_to_dec_2_out_9), .a(bin_to_dec_2_out_10), .b(bin_to_dec_2_out_11),
    .e(bin_to_dec_2_out_5), .d(bin_to_dec_2_out_6), .c(bin_to_dec_2_out_7));  // open: dp
  BCD_ADDER bcd_adder_2 (
    .C_out(bcd_adder_2_c_out), .in_1(in_1), .in_2(in_2), .in_3(in_3), .in_4(in_4), .in_5(in_21),
    .in_6(in_22), .in_7(in_23), .in_8(in_24), .out_11(bcd_adder_2_out_11), .out_12(bcd_adder_2_out_12),
    .out_13(bcd_adder_2_out_13), .out_14(bcd_adder_2_out_14), .C_in(bcd_adder_3_c_out));
  BIN_TO_DEC bin_to_dec_3 (
    .in_1(bcd_adder_3_out_11), .in_2(bcd_adder_3_out_12), .in_3(bcd_adder_3_out_13),
    .in_4(bcd_adder_3_out_14), .out_5(bin_to_dec_3_out_5), .out_6(bin_to_dec_3_out_6),
    .out_7(bin_to_dec_3_out_7), .out_8(bin_to_dec_3_out_8), .out_9(bin_to_dec_3_out_9),
    .out_10(bin_to_dec_3_out_10), .out_11(bin_to_dec_3_out_11));
  BCD_ADDER bcd_adder_3 (
    .C_out(bcd_adder_3_c_out), .in_1(in_5), .in_2(in_6), .in_3(in_7), .in_4(in_8), .in_5(in_25),
    .in_6(in_26), .in_7(in_27), .in_8(in_28), .out_11(bcd_adder_3_out_11), .out_12(bcd_adder_3_out_12),
    .out_13(bcd_adder_3_out_13), .out_14(bcd_adder_3_out_14), .C_in(bcd_adder_4_c_out));
  BIN_TO_DEC bin_to_dec_4 (
    .in_1(bcd_adder_4_out_11), .in_2(bcd_adder_4_out_12), .in_3(bcd_adder_4_out_13),
    .in_4(bcd_adder_4_out_14), .out_5(bin_to_dec_4_out_5), .out_6(bin_to_dec_4_out_6),
    .out_7(bin_to_dec_4_out_7), .out_8(bin_to_dec_4_out_8), .out_9(bin_to_dec_4_out_9),
    .out_10(bin_to_dec_4_out_10), .out_11(bin_to_dec_4_out_11));
  _7_Segment_Display u_7_segment_display_3 (
    .g(bin_to_dec_3_out_8), .f(bin_to_dec_3_out_9), .a(bin_to_dec_3_out_10), .b(bin_to_dec_3_out_11),
    .e(bin_to_dec_3_out_5), .d(bin_to_dec_3_out_6), .c(bin_to_dec_3_out_7));  // open: dp
  BCD_ADDER bcd_adder_4 (
    .C_out(bcd_adder_4_c_out), .in_1(in_9), .in_2(in_10), .in_3(in_11), .in_4(in_12), .in_5(in_29),
    .in_6(in_30), .in_7(in_31), .in_8(in_32), .out_11(bcd_adder_4_out_11), .out_12(bcd_adder_4_out_12),
    .out_13(bcd_adder_4_out_13), .out_14(bcd_adder_4_out_14), .C_in(bcd_adder_5_c_out));
  _7_Segment_Display u_7_segment_display_4 (
    .g(bin_to_dec_4_out_8), .f(bin_to_dec_4_out_9), .a(bin_to_dec_4_out_10), .b(bin_to_dec_4_out_11),
    .e(bin_to_dec_4_out_5), .d(bin_to_dec_4_out_6), .c(bin_to_dec_4_out_7));  // open: dp
  BCD_ADDER bcd_adder_5 (
    .C_out(bcd_adder_5_c_out), .in_1(in_13), .in_2(in_14), .in_3(in_15), .in_4(in_16), .in_5(in_33),
    .in_6(in_34), .in_7(in_35), .in_8(in_36), .out_11(bcd_adder_5_out_11), .out_12(bcd_adder_5_out_12),
    .out_13(bcd_adder_5_out_13), .out_14(bcd_adder_5_out_14), .C_in(bcd_adder_6_c_out));
  BIN_TO_DEC bin_to_dec_5 (
    .in_1(bcd_adder_5_out_11), .in_2(bcd_adder_5_out_12), .in_3(bcd_adder_5_out_13),
    .in_4(bcd_adder_5_out_14), .out_5(bin_to_dec_5_out_5), .out_6(bin_to_dec_5_out_6),
    .out_7(bin_to_dec_5_out_7), .out_8(bin_to_dec_5_out_8), .out_9(bin_to_dec_5_out_9),
    .out_10(bin_to_dec_5_out_10), .out_11(bin_to_dec_5_out_11));
  _7_Segment_Display u_7_segment_display_5 (
    .g(bin_to_dec_5_out_8), .f(bin_to_dec_5_out_9), .a(bin_to_dec_5_out_10), .b(bin_to_dec_5_out_11),
    .e(bin_to_dec_5_out_5), .d(bin_to_dec_5_out_6), .c(bin_to_dec_5_out_7));  // open: dp
  BCD_ADDER bcd_adder_6 (
    .C_out(bcd_adder_6_c_out), .in_1(in_17), .in_2(in_18), .in_3(in_19), .in_4(in_20), .in_5(in_37),
    .in_6(in_38), .in_7(in_39), .in_8(in_40), .out_11(bcd_adder_6_out_11), .out_12(bcd_adder_6_out_12),
    .out_13(bcd_adder_6_out_13), .out_14(bcd_adder_6_out_14), .C_in(1'b0));
  BIN_TO_DEC bin_to_dec_6 (
    .in_1(bcd_adder_6_out_11), .in_2(bcd_adder_6_out_12), .in_3(bcd_adder_6_out_13),
    .in_4(bcd_adder_6_out_14), .out_5(bin_to_dec_6_out_5), .out_6(bin_to_dec_6_out_6),
    .out_7(bin_to_dec_6_out_7), .out_8(bin_to_dec_6_out_8), .out_9(bin_to_dec_6_out_9),
    .out_10(bin_to_dec_6_out_10), .out_11(bin_to_dec_6_out_11));
  _7_Segment_Display u_7_segment_display_6 (
    .g(bin_to_dec_6_out_8), .f(bin_to_dec_6_out_9), .a(bin_to_dec_6_out_10), .b(bin_to_dec_6_out_11),
    .e(bin_to_dec_6_out_5), .d(bin_to_dec_6_out_6), .c(bin_to_dec_6_out_7));  // open: dp
endmodule

module GREATER (
  input  I_5,
  input  I_4,
  input  I_3,
  input  I_2,
  input  I_1,
  input  I2_5,
  input  I2_4,
  input  I2_3,
  input  I2_2,
  input  I2_1,
  output O_L,
  output O_R,
  output O_E
);

  wire and_1_out, and_2_out, and_3_out, and_4_out, and_5_out, and_6_out, and_8_out, and_9_out, and_10_out,
       and_11_out, and_12_out, and_13_out, and_14_out, and_15_out, and_16_out, and_17_out, and_18_out,
       and_19_out, not_1_out, not_2_out, not_3_out, not_4_out, not_5_out, not_6_out, not_7_out, not_8_out,
       not_9_out, not_10_out, not_11_out, not_12_out, not_13_out, not_14_out, not_15_out, not_16_out,
       not_17_out, not_18_out, not_19_out, not_20_out, xnor_1_out, xnor_2_out, xnor_3_out, xnor_4_out,
       xnor_5_out;

  not not_1 (not_1_out, I2_5);
  not not_2 (not_2_out, xnor_1_out);
  not not_3 (not_3_out, xnor_1_out);
  and and_1 (and_1_out, not_3_out, I_5, not_1_out);
  not not_4 (not_4_out, I_5);
  and and_2 (and_2_out, not_2_out, I2_5, not_4_out);
  xnor xnor_1 (xnor_1_out, I_5, I2_5);
  and and_3 (and_3_out, xnor_1_out, I_4);
  not not_5 (not_5_out, xnor_2_out);
  and and_4 (and_4_out, not_5_out, and_3_out, not_8_out);
  or or_1 (O_L, and_1_out, and_4_out, and_9_out, and_15_out, and_17_out);
  and and_5 (and_5_out, xnor_1_out, I2_4);
  not not_6 (not_6_out, xnor_2_out);
  not not_7 (not_7_out, and_3_out);
  not not_8 (not_8_out, and_5_out);
  and and_6 (and_6_out, not_6_out, and_5_out, not_7_out);
  and and_7 (O_E, xnor_1_out, xnor_2_out, xnor_3_out, xnor_4_out, xnor_5_out);
  or or_2 (O_R, and_2_out, and_6_out, and_11_out, and_14_out, and_19_out);
  xnor xnor_2 (xnor_2_out, and_3_out, and_5_out);
  and and_8 (and_8_out, xnor_2_out, xnor_1_out, I_3);
  not not_9 (not_9_out, and_10_out);
  not not_10 (not_10_out, xnor_3_out);
  and and_9 (and_9_out, not_10_out, and_8_out, not_9_out);
  and and_10 (and_10_out, xnor_2_out, xnor_1_out, I2_3);
  not not_11 (not_11_out, xnor_3_out);
  not not_12 (not_12_out, and_8_out);
  and and_11 (and_11_out, not_11_out, and_10_out, not_12_out);
  and and_12 (and_12_out, xnor_3_out, xnor_2_out, xnor_1_out, I_2);
  not not_13 (not_13_out, xnor_4_out);
  xnor xnor_3 (xnor_3_out, and_8_out, and_10_out);
  and and_13 (and_13_out, xnor_3_out, xnor_2_out, xnor_1_out, I2_2);
  not not_14 (not_14_out, xnor_4_out);
  not not_15 (not_15_out, and_13_out);
  and and_14 (and_14_out, not_14_out, and_13_out, not_16_out);
  and and_15 (and_15_out, not_13_out, and_12_out, not_15_out);
  not not_16 (not_16_out, and_12_out);
  xnor xnor_4 (xnor_4_out, and_12_out, and_13_out);
  and and_16 (and_16_out, xnor_4_out, xnor_3_out, xnor_2_out, xnor_1_out, I_1);
  not not_17 (not_17_out, xnor_5_out);
  not not_18 (not_18_out, and_18_out);
  and and_17 (and_17_out, not_17_out, and_16_out, not_18_out);
  and and_18 (and_18_out, xnor_4_out, xnor_3_out, xnor_2_out, xnor_1_out, I2_1);
  not not_19 (not_19_out, xnor_5_out);
  not not_20 (not_20_out, and_16_out);
  and and_19 (and_19_out, not_19_out, and_18_out, not_20_out);
  xnor xnor_5 (xnor_5_out, and_16_out, and_18_out);
endmodule

module _3_IN_ADD (
  input  in_1,
  input  in_2,
  input  in_3,
  input  in_4,
  input  in_5,
  input  in_6,
  input  in_7,
  input  in_8,
  input  in_9,
  output out_10,
  output out_11,
  output out_12,
  output out_13,
  output out_14
);

  wire full_adder_1_c_out, full_adder_2_c_out, full_adder_3_c_out;

  Full_Adder full_adder_1 (.A(in_4), .B(in_8), .C_in(in_9), .C_Out(full_adder_1_c_out), .S(out_14));
  Full_Adder full_adder_2 (.A(in_3), .B(in_7), .C_in(full_adder_1_c_out), .C_Out(full_adder_2_c_out), .S(out_13));
  Full_Adder full_adder_3 (.A(in_2), .B(in_6), .C_in(full_adder_2_c_out), .C_Out(full_adder_3_c_out), .S(out_12));
  Full_Adder full_adder_4 (.A(in_1), .B(in_5), .C_in(full_adder_3_c_out), .C_Out(out_10), .S(out_11));
endmodule

module Full_Adder (
  input  A,
  input  B,
  input  C_in,
  output C_Out,
  output S
);

  wire and_1_out, and_2_out, xor_1_out;

  and and_1 (and_1_out, B, A);
  xor xor_1 (xor_1_out, A, B);
  xor xor_2 (S, C_in, xor_1_out);
  and and_2 (and_2_out, xor_1_out, C_in);
  or or_1 (C_Out, and_2_out, and_1_out);
endmodule

module SWITCH (
  input  Toggle,
  input  in_2,
  input  in_3,
  input  in_4,
  input  in_5,
  input  in_6,
  output out_7,
  output out_8,
  output out_9,
  output out_10,
  output out_11
);

  and and_1 (out_7, Toggle, in_2);
  and and_2 (out_8, Toggle, in_3);
  and and_3 (out_9, Toggle, in_4);
  and and_4 (out_10, Toggle, in_5);
  and and_5 (out_11, Toggle, in_6);
endmodule

module BCD_ADDER (
  input  in_1,
  input  in_2,
  input  in_3,
  input  in_4,
  input  in_5,
  input  in_6,
  input  in_7,
  input  in_8,
  input  C_in,
  output C_out,
  output out_11,
  output out_12,
  output out_13,
  output out_14
);

  wire greater_1_o_e, greater_1_o_l, greater_1_o_r, n3_in_add_1_out_10, n3_in_add_1_out_11,
       n3_in_add_1_out_12, n3_in_add_1_out_13, n3_in_add_1_out_14, subtractor_1_out_6, subtractor_1_out_7,
       subtractor_1_out_8, subtractor_1_out_9, subtractor_1_out_10, switch_1_out_7, switch_1_out_8,
       switch_1_out_9, switch_1_out_10, switch_1_out_11, switch_2_out_7, switch_2_out_8, switch_2_out_9,
       switch_2_out_10, switch_2_out_11;

  _3_IN_ADD u_3_in_add_1 (
    .in_1(in_1), .in_2(in_2), .in_3(in_3), .in_4(in_4), .in_5(in_5), .in_6(in_6), .in_7(in_7), .in_8(in_8),
    .in_9(C_in), .out_10(n3_in_add_1_out_10), .out_11(n3_in_add_1_out_11), .out_12(n3_in_add_1_out_12),
    .out_13(n3_in_add_1_out_13), .out_14(n3_in_add_1_out_14));
  or or_1 (C_out, greater_1_o_l, greater_1_o_e);
  SUBTRACTOR subtractor_1 (
    .in_1(n3_in_add_1_out_10), .in_2(n3_in_add_1_out_11), .in_3(n3_in_add_1_out_12),
    .in_4(n3_in_add_1_out_13), .in_5(n3_in_add_1_out_14), .out_6(subtractor_1_out_6),
    .out_7(subtractor_1_out_7), .out_8(subtractor_1_out_8), .out_9(subtractor_1_out_9),
    .out_10(subtractor_1_out_10));
  SWITCH switch_1 (
    .Toggle(C_out), .in_2(subtractor_1_out_6), .in_3(subtractor_1_out_7), .in_4(subtractor_1_out_8),
    .in_5(subtractor_1_out_9), .in_6(subtractor_1_out_10), .out_7(switch_1_out_7), .out_8(switch_1_out_8),
    .out_9(switch_1_out_9), .out_10(switch_1_out_10), .out_11(switch_1_out_11));
  GREATER greater_1 (
    .I_5(n3_in_add_1_out_10), .I_4(n3_in_add_1_out_11), .I_3(n3_in_add_1_out_12), .I_2(n3_in_add_1_out_13),
    .I_1(n3_in_add_1_out_14), .I2_5(1'b0), .I2_4(1'b1), .I2_3(1'b0), .I2_2(1'b1), .I2_1(1'b0),
    .O_L(greater_1_o_l), .O_R(greater_1_o_r), .O_E(greater_1_o_e));
  or or_2 (out_11, switch_1_out_8, switch_2_out_8);
  // OR_Gate or_3 has open pins: in0=switch_1_out_7, in1=switch_2_out_7, out=open
  SWITCH switch_2 (
    .Toggle(greater_1_o_r), .in_2(n3_in_add_1_out_10), .in_3(n3_in_add_1_out_11), .in_4(n3_in_add_1_out_12),
    .in_5(n3_in_add_1_out_13), .in_6(n3_in_add_1_out_14), .out_7(switch_2_out_7), .out_8(switch_2_out_8),
    .out_9(switch_2_out_9), .out_10(switch_2_out_10), .out_11(switch_2_out_11));
  or or_4 (out_12, switch_1_out_9, switch_2_out_9);
  or or_5 (out_13, switch_1_out_10, switch_2_out_10);
  or or_6 (out_14, switch_1_out_11, switch_2_out_11);
endmodule

module SUBTRACTOR (
  input  in_1,
  input  in_2,
  input  in_3,
  input  in_4,
  input  in_5,
  output out_6,
  output out_7,
  output out_8,
  output out_9,
  output out_10
);

  wire subtractor_1_bout, subtractor_2_bout, subtractor_3_bout, subtractor_4_bout;

  Subtractor #(.width(1)) subtractor_1 (.a(in_5), .b(1'b0), .out(out_10), .bin(1'b0), .bout(subtractor_1_bout));
  Subtractor #(.width(1)) subtractor_2 (
    .a(in_4), .b(1'b1), .out(out_9), .bin(subtractor_1_bout), .bout(subtractor_2_bout));
  Subtractor #(.width(1)) subtractor_3 (
    .a(in_3), .b(1'b0), .out(out_8), .bin(subtractor_2_bout), .bout(subtractor_3_bout));
  Subtractor #(.width(1)) subtractor_4 (
    .a(in_2), .b(1'b1), .out(out_7), .bin(subtractor_3_bout), .bout(subtractor_4_bout));
  Subtractor #(.width(1)) subtractor_5 (.a(in_1), .b(1'b0), .out(out_6), .bin(subtractor_4_bout));  // open: bout
endmodule

module BIN_TO_DEC (
  input  in_1,
  input  in_2,
  input  in_3,
  input  in_4,
  output out_5,
  output out_6,
  output out_7,
  output out_8,
  output out_9,
  output out_10,
  output out_11
);

  wire and_1_out, and_2_out, and_3_out, and_4_out, and_5_out, and_6_out, and_7_out, and_8_out, and_9_out,
       and_10_out, not_1_out, not_2_out, not_3_out, not_4_out, not_5_out, not_6_out, not_7_out, not_8_out,
       not_9_out, not_10_out, not_11_out, not_12_out, not_13_out, not_14_out, not_15_out, not_16_out,
       not_17_out, not_18_out, not_19_out, not_20_out, not_21_out, not_22_out, not_23_out, not_24_out,
       not_25_out;

  and and_1 (and_1_out, not_1_out, not_4_out, not_3_out, not_5_out);
  not not_1 (not_1_out, in_1);
  not not_2 (not_2_out, in_1);
  not not_3 (not_3_out, in_3);
  not not_4 (not_4_out, in_2);
  not not_5 (not_5_out, in_4);
  and and_2 (and_2_out, not_8_out, not_9_out, in_3, not_11_out);
  and and_3 (and_3_out, not_2_out, not_7_out, not_6_out, in_4);
  not not_6 (not_6_out, in_3);
  not not_7 (not_7_out, in_2);
  not not_8 (not_8_out, in_1);
  not not_9 (not_9_out, in_2);
  and and_4 (and_4_out, not_10_out, not_12_out, in_3, in_4);
  not not_10 (not_10_out, in_1);
  not not_11 (not_11_out, in_4);
  not not_12 (not_12_out, in_2);
  and and_5 (and_5_out, not_15_out, in_2, not_14_out, not_13_out);
  not not_13 (not_13_out, in_4);
  not not_14 (not_14_out, in_3);
  not not_15 (not_15_out, in_1);
  not not_16 (not_16_out, in_1);
  and and_6 (and_6_out, not_18_out, in_2, in_3, not_19_out);
  and and_7 (and_7_out, not_16_out, in_2, not_17_out, in_4);
  not not_17 (not_17_out, in_3);
  not not_18 (not_18_out, in_1);
  and and_8 (and_8_out, not_20_out, in_2, in_3, in_4);
  not not_19 (not_19_out, in_4);
  not not_20 (not_20_out, in_1);
  and and_9 (and_9_out, in_1, not_21_out, not_23_out, not_22_out);
  not not_21 (not_21_out, in_2);
  not not_22 (not_22_out, in_4);
  not not_23 (not_23_out, in_3);
  and and_10 (and_10_out, in_1, not_25_out, not_24_out, in_4);
  not not_24 (not_24_out, in_3);
  not not_25 (not_25_out, in_2);
  or or_1 (out_8, and_2_out, and_4_out, and_5_out, and_6_out, and_7_out, and_9_out, and_10_out);
  or or_2 (out_9, and_1_out, and_5_out, and_7_out, and_6_out, and_9_out, and_10_out);
  or or_3 (out_10, and_1_out, and_2_out, and_4_out, and_7_out, and_6_out, and_8_out, and_9_out, and_10_out);
  or or_4 (out_11, and_1_out, and_3_out, and_2_out, and_4_out, and_5_out, and_8_out, and_9_out, and_10_out);
  or or_5 (out_7, and_1_out, and_3_out, and_4_out, and_5_out, and_7_out, and_6_out, and_8_out, and_9_out, and_10_out);
  or or_6 (out_6, and_1_out, and_2_out, and_4_out, and_6_out, and_7_out, and_9_out, and_10_out);
  or or_7 (out_5, and_1_out, and_2_out, and_6_out, and_9_out);
endmodule
