// Logisim project Divide.circ as structural Verilog: 4 circuits, main circuit main
module main (
  input  in_1,
  input  in_2,
  input  in_3,
  input  in_4,
  input  in_5,
  input  in_6,
  input  in_7,
  input  in_8,
  output out_9,
  output out_10,
  output out_11,
  output out_12,
  output out_13,
  output out_14,
  output out_15,
  output out_16
);

  wire div_1_out_5, div_1_out_6, div_1_out_8, div_2_out_5, div_2_out_6, div_2_out_7, div_2_out_8,
       div_3_out_5, div_3_out_6, div_3_out_8, div_4_out_5, div_4_out_6, div_4_out_8, div_5_out_5,
       div_5_out_6, div_5_out_7, div_5_out_8, div_6_out_5, div_6_out_7, div_6_out_8, div_7_out_5,
       div_7_out_6, div_7_out_7, div_7_out_8, div_8_out_5, div_8_out_7, div_8_out_8, div_9_out_5,
       div_9_out_6, div_9_out_7, div_9_out_8, div_10_out_5, div_10_out_6, div_10_out_7, div_10_out_8,
       div_11_out_5, div_11_out_6, div_11_out_7, div_11_out_8, div_12_out_5, div_12_out_6, div_13_out_5,
       div_13_out_6, div_14_out_5, div_14_out_6, div_15_out_5, div_15_out_7, div_15_out_8, div_16_out_5;

  not not_1 (out_9, div_1_out_5);
  Div div_1 (
    .out_5(div_1_out_5), .in_4(div_1_out_5), .in_1(in_1), .in_2(1'b0), .out_8(div_1_out_8),
    .in_3(div_2_out_5), .out_6(div_1_out_6));  // open: out_7
  Div div_2 (
    .out_5(div_2_out_5), .in_4(div_1_out_6), .in_1(in_2), .in_2(1'b0), .out_7(div_2_out_7),
    .out_8(div_2_out_8), .in_3(div_5_out_5), .out_6(div_2_out_6));
  Div div_3 (
    .out_5(div_3_out_5), .in_4(div_3_out_5), .in_1(div_1_out_8), .in_2(div_2_out_7), .out_8(div_3_out_8),
    .in_3(div_7_out_5), .out_6(div_3_out_6));  // open: out_7
  Div div_4 (
    .out_5(div_4_out_5), .in_4(div_4_out_5), .in_1(div_3_out_8), .in_2(div_7_out_7), .out_8(div_4_out_8),
    .in_3(div_11_out_5), .out_6(div_4_out_6));  // open: out_7
  not not_2 (out_11, div_4_out_5);
  not not_3 (out_10, div_3_out_5);
  not not_4 (out_12, div_12_out_5);
  Div div_5 (
    .out_5(div_5_out_5), .in_4(div_2_out_6), .in_1(in_3), .in_2(1'b0), .out_7(div_5_out_7),
    .out_8(div_5_out_8), .in_3(div_6_out_5), .out_6(div_5_out_6));
  Div div_6 (
    .out_5(div_6_out_5), .in_4(div_5_out_6), .in_1(in_4), .in_2(in_5), .out_7(div_6_out_7),
    .out_8(div_6_out_8), .in_3(1'b0));  // open: out_6
  Div div_7 (
    .out_5(div_7_out_5), .in_4(div_3_out_6), .in_1(div_2_out_8), .in_2(div_5_out_7), .out_7(div_7_out_7),
    .out_8(div_7_out_8), .in_3(div_9_out_5), .out_6(div_7_out_6));
  Div div_8 (
    .out_5(div_8_out_5), .in_4(div_9_out_6), .in_1(div_6_out_8), .in_2(in_6), .out_7(div_8_out_7),
    .out_8(div_8_out_8), .in_3(1'b0));  // open: out_6
  Div div_9 (
    .out_5(div_9_out_5), .in_4(div_7_out_6), .in_1(div_5_out_8), .in_2(div_6_out_7), .out_7(div_9_out_7),
    .out_8(div_9_out_8), .in_3(div_8_out_5), .out_6(div_9_out_6));
  Div div_10 (
    .out_5(div_10_out_5), .in_4(div_11_out_6), .in_1(div_9_out_8), .in_2(div_8_out_7), .out_7(div_10_out_7),
    .out_8(div_10_out_8), .in_3(div_15_out_5), .out_6(div_10_out_6));
  Div div_11 (
    .out_5(div_11_out_5), .in_4(div_4_out_6), .in_1(div_7_out_8), .in_2(div_9_out_7), .out_7(div_11_out_7),
    .out_8(div_11_out_8), .in_3(div_10_out_5), .out_6(div_11_out_6));
  Div div_12 (
    .out_5(div_12_out_5), .in_4(div_12_out_5), .in_1(div_4_out_8), .in_2(div_11_out_7), .out_7(out_13),
    .in_3(div_14_out_5), .out_6(div_12_out_6));  // open: out_8
  Div div_13 (
    .out_5(div_13_out_5), .in_4(div_14_out_6), .in_1(div_10_out_8), .in_2(div_15_out_7), .out_7(out_15),
    .in_3(div_16_out_5), .out_6(div_13_out_6));  // open: out_8
  Div div_14 (
    .out_5(div_14_out_5), .in_4(div_12_out_6), .in_1(div_11_out_8), .in_2(div_10_out_7), .out_7(out_14),
    .in_3(div_13_out_5), .out_6(div_14_out_6));  // open: out_8
  Div div_15 (
    .out_5(div_15_out_5), .in_4(div_10_out_6), .in_1(div_8_out_8), .in_2(in_7), .out_7(div_15_out_7),
    .out_8(div_15_out_8), .in_3(1'b0));  // open: out_6
  Div div_16 (
    .out_5(div_16_out_5), .in_4(div_13_out_6), .in_1(div_15_out_8), .in_2(in_8), .out_7(out_16), .in_3(1'b0));  // open: out_8, out_6
endmodule

module sub (
  input  in_1,
  input  in_2,
  input  in_3,
  output out_4,
  output out_5
);

  wire and_1_out, and_2_out, not_1_out, not_2_out, xor_1_out;

  or or_1 (out_4, and_1_out, and_2_out);
  not not_1 (not_1_out, in_2);
  and and_1 (and_1_out, not_1_out, in_1);
  not not_2 (not_2_out, xor_1_out);
  and and_2 (and_2_out, not_2_out, in_3);
  xor xor_1 (xor_1_out, in_1, in_2);
  xor xor_2 (out_5, in_3, xor_1_out);
endmodule

module add (
  input  in_1,
  input  in_2,
  input  in_3,
  output out_4,
  output out_5
);

  wire and_1_out, and_2_out, xor_1_out;

  or or_1 (out_4, and_1_out, and_2_out);
  and and_1 (and_1_out, in_2, in_1);
  and and_2 (and_2_out, xor_1_out, in_3);
  xor xor_1 (xor_1_out, in_1, in_2);
  xor xor_2 (out_5, in_3, xor_1_out);
endmodule

module Div (
  input  in_1,
  input  in_2,
  input  in_3,
  input  in_4,
  output out_5,
  output out_6,
  output out_7,
  output out_8
);

  wire and_1_out, and_2_out, not_1_out, sub_1_out_5;

  sub sub_1 (.out_4(out_5), .in_1(in_1), .in_2(in_2), .out_5(sub_1_out_5), .in_3(in_3));
  and and_1 (and_1_out, sub_1_out_5, in_4);
  not not_1 (not_1_out, in_4);
  and and_2 (and_2_out, in_2, not_1_out);
  or or_1 (out_7, and_1_out, and_2_out);

  assign out_6 = in_4;
  assign out_8 = in_1;
endmodule
