// Logisim project Input_Count.circ as structural Verilog: 3 circuits, main circuit main
module main (
  input  in_1,
  input  in_2,
  input  in_3,
  input  in_4,
  input  in_5,
  input  in_6,
  input  in_7,
  output out_8,
  output out_9,
  output out_10,
  output out_11
);

  wire fulladd_1_out_4, fulladd_1_out_5, fulladd_2_out_4, fulladd_2_out_5, fulladd_3_out_4, halfadd_1_out_3,
       halfadd_1_out_4, halfadd_3_out_3;

  HalfAdd halfadd_1 (.out_3(halfadd_1_out_3), .in_2(fulladd_2_out_4), .in_1(fulladd_1_out_4), .out_4(halfadd_1_out_4));
  HalfAdd halfadd_2 (.out_3(out_8), .in_2(halfadd_3_out_3), .in_1(halfadd_1_out_3), .out_4(out_9));
  HalfAdd halfadd_3 (.out_3(halfadd_3_out_3), .in_2(fulladd_3_out_4), .in_1(halfadd_1_out_4), .out_4(out_10));
  FullAdd fulladd_1 (.out_4(fulladd_1_out_4), .in_3(in_5), .in_1(in_3), .in_2(in_4), .out_5(fulladd_1_out_5));
  FullAdd fulladd_2 (
    .out_4(fulladd_2_out_4), .in_3(in_6), .in_1(in_2), .in_2(fulladd_1_out_5), .out_5(fulladd_2_out_5));
  FullAdd fulladd_3 (.out_4(fulladd_3_out_4), .in_3(in_7), .in_1(in_1), .in_2(fulladd_2_out_5), .out_5(out_11));
endmodule

module FullAdd (
  input  in_1,
  input  in_2,
  input  in_3,
  output out_4,
  output out_5
);

  wire and_1_out, and_2_out, xor_1_out;

  and and_1 (and_1_out, in_1, in_2);
  or or_1 (out_4, and_1_out, and_2_out);
  and and_2 (and_2_out, in_3, xor_1_out);
  xor xor_1 (xor_1_out, in_2, in_1);
  xor xor_2 (out_5, xor_1_out, in_3);
endmodule

module HalfAdd (
  input  in_1,
  input  in_2,
  output out_3,
  output out_4
);

  and and_1 (out_3, in_1, in_2);
  xor xor_1 (out_4, in_1, in_2);
endmodule
