// Logisim project Joystick_Display.circ as structural Verilog: 4 circuits, main circuit main
module main (
  input  in_1,
  input  in_2,
  input  [1:0] in_3,
  input  [4:0] in_4,
  input  [7:0] in_5,
  input  in_6,
  input  in_7,
  output [3:0] out_8,
  output [7:0] out_9
);

  wire button_1_out, button_2_out, decode_2_out_5, decode_2_out_6, decode_2_out_7, decode_2_out_8,
       decode_2_out_9, decode_2_out_10, decode_2_out_11, decode_2_out_12, decode_2_out_13, decode_2_out_14,
       decode_2_out_15, decode_2_out_16, decode_2_out_17, decode_2_out_18, decode_2_out_19,
       demultiplexer_3_out0, demultiplexer_3_out1, demultiplexer_3_out2, demultiplexer_3_out3,
       demultiplexer_3_out4, demultiplexer_3_out5, demultiplexer_3_out6, demultiplexer_3_out7,
       demultiplexer_3_out8, demultiplexer_3_out9, demultiplexer_3_out10, demultiplexer_3_out11,
       demultiplexer_3_out12, demultiplexer_3_out13, demultiplexer_3_out14, demultiplexer_3_out15,
       demultiplexer_3_out16, demultiplexer_3_out17, demultiplexer_3_out18, demultiplexer_3_out19,
       demultiplexer_3_out20, demultiplexer_3_out21, demultiplexer_3_out22, demultiplexer_3_out23,
       demultiplexer_3_out24, demultiplexer_3_out25, demultiplexer_3_out26, demultiplexer_3_out27,
       demultiplexer_3_out28, demultiplexer_3_out29, demultiplexer_3_out30, demultiplexer_3_out31;
  wire [3:0] joystick_1_x, joystick_1_y;
  wire [4:0] joystick_2_x, joystick_2_y;
  wire [14:0] and_1_out, and_2_out, and_3_out, and_4_out, and_5_out, and_6_out, and_7_out, and_8_out,
       and_9_out, and_10_out, and_11_out, and_12_out, and_13_out, and_14_out, and_15_out, decode_1_out_19,
       extend_1_out_8, extend_1_out_9, extend_1_out_10, extend_1_out_11, extend_1_out_12, extend_1_out_13,
       extend_1_out_14, extend_2_out_8, extend_2_out_9, extend_2_out_10, extend_2_out_11, extend_2_out_12,
       extend_2_out_13, extend_2_out_14, extend_3_out_8;
  wire [30:0] and_16_out, and_17_out, and_18_out, and_19_out, and_20_out, and_21_out, and_22_out, and_23_out,
       and_24_out, and_25_out, and_26_out, and_27_out, and_28_out, and_29_out, and_30_out, and_31_out,
       and_32_out, and_33_out, and_34_out, and_35_out, and_36_out, and_37_out, and_38_out, and_39_out,
       and_40_out, and_41_out, and_42_out, and_43_out, and_44_out, and_45_out, and_46_out,
       demultiplexer_2_out31, extend2_1_out_8, extend2_1_out_9, extend2_1_out_10, extend2_1_out_11,
       extend2_1_out_12, extend2_1_out_13, extend2_1_out_14, extend2_2_out_8, extend2_2_out_9,
       extend2_2_out_10, extend2_2_out_11, extend2_2_out_12, extend2_2_out_13, extend2_2_out_14,
       extend2_3_out_8, extend2_3_out_9, extend2_3_out_10, extend2_3_out_11, extend2_3_out_12,
       extend2_3_out_13, extend2_3_out_14, extend2_4_out_8, extend2_4_out_9, extend2_4_out_10,
       extend2_4_out_11, extend2_4_out_12, extend2_4_out_13, extend2_4_out_14, extend2_5_out_8,
       extend2_5_out_9, extend2_5_out_10;

  Joystick joystick_1 (.x(joystick_1_x), .y(joystick_1_y));
  decode decode_1 (
    .in_1(joystick_1_y[0]), .in_2(joystick_1_y[1]), .in_3(joystick_1_y[2]), .in_4(joystick_1_y[3]),
    .out_5(decode_1_out_19[14]), .out_6(decode_1_out_19[13]), .out_7(decode_1_out_19[12]),
    .out_8(decode_1_out_19[11]), .out_9(decode_1_out_19[10]), .out_10(decode_1_out_19[9]),
    .out_11(decode_1_out_19[8]), .out_12(decode_1_out_19[7]), .out_13(decode_1_out_19[6]),
    .out_14(decode_1_out_19[5]), .out_15(decode_1_out_19[4]), .out_16(decode_1_out_19[3]),
    .out_17(decode_1_out_19[2]), .out_18(decode_1_out_19[1]), .out_19(decode_1_out_19[0]));
  Shift_Register shift_register_1 (
    .shift(1'b1), .in(in_7), .clk(button_1_out), .load(in_6), .clr(button_2_out), .d0(in_5[7]),
    .q0(out_9[7]), .d1(in_5[6]), .q1(out_9[6]), .d2(in_5[5]), .q2(out_9[5]), .d3(in_5[4]), .q3(out_9[4]),
    .d4(in_5[3]), .q4(out_9[3]), .d5(in_5[2]), .q5(out_9[2]), .d6(in_5[1]), .q6(out_9[1]), .d7(in_5[0]),
    .q7(out_9[0]));  // open: out
  Button button_1 (.out(button_1_out));
  Button button_2 (.out(button_2_out));
  decode decode_2 (
    .in_1(joystick_1_x[0]), .in_2(joystick_1_x[1]), .in_3(joystick_1_x[2]), .in_4(joystick_1_x[3]),
    .out_5(decode_2_out_5), .out_6(decode_2_out_6), .out_7(decode_2_out_7), .out_8(decode_2_out_8),
    .out_9(decode_2_out_9), .out_10(decode_2_out_10), .out_11(decode_2_out_11), .out_12(decode_2_out_12),
    .out_13(decode_2_out_13), .out_14(decode_2_out_14), .out_15(decode_2_out_15), .out_16(decode_2_out_16),
    .out_17(decode_2_out_17), .out_18(decode_2_out_18), .out_19(decode_2_out_19));
  extend extend_1 (
    .in_1(decode_2_out_5), .in_2(decode_2_out_6), .in_3(decode_2_out_7), .in_4(decode_2_out_8),
    .in_5(decode_2_out_9), .in_6(decode_2_out_10), .in_7(decode_2_out_11), .out_8(extend_1_out_8),
    .out_9(extend_1_out_9), .out_10(extend_1_out_10), .out_11(extend_1_out_11), .out_12(extend_1_out_12),
    .out_13(extend_1_out_13), .out_14(extend_1_out_14));
  extend extend_2 (
    .in_1(decode_2_out_12), .in_2(decode_2_out_13), .in_3(decode_2_out_14), .in_4(decode_2_out_15),
    .in_5(decode_2_out_16), .in_6(decode_2_out_17), .in_7(decode_2_out_18), .out_8(extend_2_out_8),
    .out_9(extend_2_out_9), .out_10(extend_2_out_10), .out_11(extend_2_out_11), .out_12(extend_2_out_12),
    .out_13(extend_2_out_13), .out_14(extend_2_out_14));
  extend extend_3 (
    .in_1(decode_2_out_19), .out_8(extend_3_out_8));  // open: in_2, in_3, in_4, in_5, in_6, in_7, out_9, out_10, out_11, out_12, out_13, out_14
  Demultiplexer #(.select(2)) demultiplexer_1 (
    .out0(out_8[0]), .out1(out_8[1]), .out2(out_8[2]), .out3(out_8[3]), .in(in_1), .sel(in_3), .en(in_2));
  assign and_1_out = decode_1_out_19 & extend_1_out_8;  // AND_Gate and_1, 15 bits wide
  assign and_2_out = decode_1_out_19 & extend_1_out_9;  // AND_Gate and_2, 15 bits wide
  DotMatrix #(.matrixcols(15), .matrixrows(15)) dotmatrix_1 (
    .col0(and_1_out), .col1(and_2_out), .col2(and_3_out), .col3(and_4_out), .col4(and_6_out),
    .col5(and_7_out), .col6(and_5_out), .col7(and_8_out), .col8(and_9_out), .col9(and_10_out),
    .col10(and_11_out), .col11(and_12_out), .col12(and_13_out), .col13(and_14_out), .col14(and_15_out));
  assign and_3_out = decode_1_out_19 & extend_1_out_10;  // AND_Gate and_3, 15 bits wide
  assign and_4_out = decode_1_out_19 & extend_1_out_11;  // AND_Gate and_4, 15 bits wide
  Joystick #(.bits(5)) joystick_2 (.x(joystick_2_x), .y(joystick_2_y));
  assign and_5_out = decode_1_out_19 & extend_1_out_14;  // AND_Gate and_5, 15 bits wide
  assign and_6_out = decode_1_out_19 & extend_1_out_12;  // AND_Gate and_6, 15 bits wide
  assign and_7_out = decode_1_out_19 & extend_1_out_13;  // AND_Gate and_7, 15 bits wide
  Demultiplexer #(.select(5)) demultiplexer_2 (
    .out1(demultiplexer_2_out31[30]), .out2(demultiplexer_2_out31[29]), .out3(demultiplexer_2_out31[28]),
    .out4(demultiplexer_2_out31[27]), .out5(demultiplexer_2_out31[26]), .out6(demultiplexer_2_out31[25]),
    .out7(demultiplexer_2_out31[24]), .out8(demultiplexer_2_out31[23]), .out9(demultiplexer_2_out31[22]),
    .out10(demultiplexer_2_out31[21]), .out11(demultiplexer_2_out31[20]), .out12(demultiplexer_2_out31[19]),
    .out13(demultiplexer_2_out31[18]), .out14(demultiplexer_2_out31[17]), .out15(demultiplexer_2_out31[16]),
    .out16(demultiplexer_2_out31[15]), .out17(demultiplexer_2_out31[14]), .out18(demultiplexer_2_out31[13]),
    .out19(demultiplexer_2_out31[12]), .out20(demultiplexer_2_out31[11]), .out21(demultiplexer_2_out31[10]),
    .out22(demultiplexer_2_out31[9]), .out23(demultiplexer_2_out31[8]), .out24(demultiplexer_2_out31[7]),
    .out25(demultiplexer_2_out31[6]), .out26(demultiplexer_2_out31[5]), .out27(demultiplexer_2_out31[4]),
    .out28(demultiplexer_2_out31[3]), .out29(demultiplexer_2_out31[2]), .out30(demultiplexer_2_out31[1]),
    .out31(demultiplexer_2_out31[0]), .in(1'b1), .sel(joystick_2_y), .en(1'b1));  // open: out0
  Demultiplexer #(.select(5)) demultiplexer_3 (
    .out0(demultiplexer_3_out0), .out1(demultiplexer_3_out1), .out2(demultiplexer_3_out2),
    .out3(demultiplexer_3_out3), .out4(demultiplexer_3_out4), .out5(demultiplexer_3_out5),
    .out6(demultiplexer_3_out6), .out7(demultiplexer_3_out7), .out8(demultiplexer_3_out8),
    .out9(demultiplexer_3_out9), .out10(demultiplexer_3_out10), .out11(demultiplexer_3_out11),
    .out12(demultiplexer_3_out12), .out13(demultiplexer_3_out13), .out14(demultiplexer_3_out14),
    .out15(demultiplexer_3_out15), .out16(demultiplexer_3_out16), .out17(demultiplexer_3_out17),
    .out18(demultiplexer_3_out18), .out19(demultiplexer_3_out19), .out20(demultiplexer_3_out20),
    .out21(demultiplexer_3_out21), .out22(demultiplexer_3_out22), .out23(demultiplexer_3_out23),
    .out24(demultiplexer_3_out24), .out25(demultiplexer_3_out25), .out26(demultiplexer_3_out26),
    .out27(demultiplexer_3_out27), .out28(demultiplexer_3_out28), .out29(demultiplexer_3_out29),
    .out30(demultiplexer_3_out30), .out31(demultiplexer_3_out31), .in(1'b1), .sel(joystick_2_x), .en(1'b1));
  assign and_8_out = decode_1_out_19 & extend_2_out_8;  // AND_Gate and_8, 15 bits wide
  assign and_9_out = decode_1_out_19 & extend_2_out_9;  // AND_Gate and_9, 15 bits wide
  assign and_10_out = decode_1_out_19 & extend_2_out_10;  // AND_Gate and_10, 15 bits wide
  extend2 extend2_1 (
    .in_1(demultiplexer_3_out0), .in_2(demultiplexer_3_out1), .in_3(demultiplexer_3_out2),
    .in_4(demultiplexer_3_out3), .in_5(demultiplexer_3_out4), .in_6(demultiplexer_3_out5),
    .in_7(demultiplexer_3_out6), .out_8(extend2_1_out_8), .out_9(extend2_1_out_9), .out_10(extend2_1_out_10),
    .out_11(extend2_1_out_11), .out_12(extend2_1_out_12), .out_13(extend2_1_out_13), .out_14(extend2_1_out_14));
  extend2 extend2_2 (
    .in_1(demultiplexer_3_out7), .in_2(demultiplexer_3_out8), .in_3(demultiplexer_3_out9),
    .in_4(demultiplexer_3_out10), .in_5(demultiplexer_3_out11), .in_6(demultiplexer_3_out12),
    .in_7(demultiplexer_3_out13), .out_8(extend2_2_out_8), .out_9(extend2_2_out_9),
    .out_10(extend2_2_out_10), .out_11(extend2_2_out_11), .out_12(extend2_2_out_12),
    .out_13(extend2_2_out_13), .out_14(extend2_2_out_14));
  extend2 extend2_3 (
    .in_1(demultiplexer_3_out14), .in_2(demultiplexer_3_out15), .in_3(demultiplexer_3_out16),
    .in_4(demultiplexer_3_out17), .in_5(demultiplexer_3_out18), .in_6(demultiplexer_3_out19),
    .in_7(demultiplexer_3_out20), .out_8(extend2_3_out_8), .out_9(extend2_3_out_9),
    .out_10(extend2_3_out_10), .out_11(extend2_3_out_11), .out_12(extend2_3_out_12),
    .out_13(extend2_3_out_13), .out_14(extend2_3_out_14));
  extend2 extend2_4 (
    .in_1(demultiplexer_3_out21), .in_2(demultiplexer_3_out22), .in_3(demultiplexer_3_out23),
    .in_4(demultiplexer_3_out24), .in_5(demultiplexer_3_out25), .in_6(demultiplexer_3_out26),
    .in_7(demultiplexer_3_out27), .out_8(extend2_4_out_8), .out_9(extend2_4_out_9),
    .out_10(extend2_4_out_10), .out_11(extend2_4_out_11), .out_12(extend2_4_out_12),
    .out_13(extend2_4_out_13), .out_14(extend2_4_out_14));
  extend2 extend2_5 (
    .in_1(demultiplexer_3_out28), .in_2(demultiplexer_3_out29), .in_3(demultiplexer_3_out30),
    .in_4(demultiplexer_3_out31), .out_8(extend2_5_out_8), .out_9(extend2_5_out_9), .out_10(extend2_5_out_10));  // open: in_5, in_6, in_7, out_11, out_12, out_13, out_14
  assign and_11_out = decode_1_out_19 & extend_2_out_11;  // AND_Gate and_11, 15 bits wide
  assign and_12_out = decode_1_out_19 & extend_2_out_12;  // AND_Gate and_12, 15 bits wide
  assign and_13_out = decode_1_out_19 & extend_2_out_13;  // AND_Gate and_13, 15 bits wide
  assign and_14_out = decode_1_out_19 & extend_2_out_14;  // AND_Gate and_14, 15 bits wide
  assign and_15_out = decode_1_out_19 & extend_3_out_8;  // AND_Gate and_15, 15 bits wide
  DotMatrix #(.matrixcols(31), .matrixrows(31)) dotmatrix_2 (
    .col0(and_16_out), .col1(and_18_out), .col2(and_17_out), .col3(and_19_out), .col4(and_20_out),
    .col5(and_21_out), .col6(and_23_out), .col7(and_24_out), .col8(and_22_out), .col9(and_26_out),
    .col10(and_25_out), .col11(and_29_out), .col12(and_28_out), .col13(and_27_out), .col14(and_31_out),
    .col15(and_30_out), .col16(and_32_out), .col17(and_34_out), .col18(and_33_out), .col19(and_37_out),
    .col20(and_35_out), .col21(and_36_out), .col22(and_39_out), .col23(and_40_out), .col24(and_38_out),
    .col25(and_42_out), .col26(and_41_out), .col27(and_45_out), .col28(and_44_out), .col29(and_43_out),
    .col30(and_46_out));
  assign and_16_out = demultiplexer_2_out31 & extend2_1_out_8;  // AND_Gate and_16, 31 bits wide
  assign and_17_out = demultiplexer_2_out31 & extend2_1_out_10;  // AND_Gate and_17, 31 bits wide
  assign and_18_out = demultiplexer_2_out31 & extend2_1_out_9;  // AND_Gate and_18, 31 bits wide
  assign and_19_out = demultiplexer_2_out31 & extend2_1_out_11;  // AND_Gate and_19, 31 bits wide
  assign and_20_out = demultiplexer_2_out31 & extend2_1_out_12;  // AND_Gate and_20, 31 bits wide
  assign and_21_out = demultiplexer_2_out31 & extend2_1_out_13;  // AND_Gate and_21, 31 bits wide
  assign and_22_out = demultiplexer_2_out31 & extend2_2_out_9;  // AND_Gate and_22, 31 bits wide
  assign and_23_out = demultiplexer_2_out31 & extend2_1_out_14;  // AND_Gate and_23, 31 bits wide
  assign and_24_out = demultiplexer_2_out31 & extend2_2_out_8;  // AND_Gate and_24, 31 bits wide
  assign and_25_out = demultiplexer_2_out31 & extend2_2_out_11;  // AND_Gate and_25, 31 bits wide
  assign and_26_out = demultiplexer_2_out31 & extend2_2_out_10;  // AND_Gate and_26, 31 bits wide
  assign and_27_out = demultiplexer_2_out31 & extend2_2_out_14;  // AND_Gate and_27, 31 bits wide
  assign and_28_out = demultiplexer_2_out31 & extend2_2_out_13;  // AND_Gate and_28, 31 bits wide
  assign and_29_out = demultiplexer_2_out31 & extend2_2_out_12;  // AND_Gate and_29, 31 bits wide
  assign and_30_out = demultiplexer_2_out31 & extend2_3_out_9;  // AND_Gate and_30, 31 bits wide
  assign and_31_out = demultiplexer_2_out31 & extend2_3_out_8;  // AND_Gate and_31, 31 bits wide
  assign and_32_out = demultiplexer_2_out31 & extend2_3_out_10;  // AND_Gate and_32, 31 bits wide
  assign and_33_out = demultiplexer_2_out31 & extend2_3_out_12;  // AND_Gate and_33, 31 bits wide
  assign and_34_out = demultiplexer_2_out31 & extend2_3_out_11;  // AND_Gate and_34, 31 bits wide
  assign and_35_out = demultiplexer_2_out31 & extend2_3_out_14;  // AND_Gate and_35, 31 bits wide
  assign and_36_out = demultiplexer_2_out31 & extend2_4_out_8;  // AND_Gate and_36, 31 bits wide
  assign and_37_out = demultiplexer_2_out31 & extend2_3_out_13;  // AND_Gate and_37, 31 bits wide
  assign and_38_out = demultiplexer_2_out31 & extend2_4_out_11;  // AND_Gate and_38, 31 bits wide
  assign and_39_out = demultiplexer_2_out31 & extend2_4_out_9;  // AND_Gate and_39, 31 bits wide
  assign and_40_out = demultiplexer_2_out31 & extend2_4_out_10;  // AND_Gate and_40, 31 bits wide
  assign and_41_out = demultiplexer_2_out31 & extend2_4_out_13;  // AND_Gate and_41, 31 bits wide
  assign and_42_out = demultiplexer_2_out31 & extend2_4_out_12;  // AND_Gate and_42, 31 bits wide
  assign and_43_out = demultiplexer_2_out31 & extend2_5_out_9;  // AND_Gate and_43, 31 bits wide
  assign and_44_out = demultiplexer_2_out31 & extend2_5_out_8;  // AND_Gate and_44, 31 bits wide
  assign and_45_out = demultiplexer_2_out31 & extend2_4_out_14;  // AND_Gate and_45, 31 bits wide
  assign and_46_out = demultiplexer_2_out31 & extend2_5_out_10;  // AND_Gate and_46, 31 bits wide
endmodule

module decode (
  input  in_1,
  input  in_2,
  input  in_3,
  input  in_4,
  output out_5,
  output out_6,
  output out_7,
  output out_8,
  output out_9,
  output out_10,
  output out_11,
  output out_12,
  output out_13,
  output out_14,
  output out_15,
  output out_16,
  output out_17,
  output out_18,
  output out_19
);

  and and_1 (out_5, ~in_4, ~in_3, ~in_2, in_1);  // AND_Gate
  and and_2 (out_7, ~in_4, ~in_3, in_2, in_1);  // AND_Gate
  and and_3 (out_6, ~in_4, ~in_3, in_2, ~in_1);  // AND_Gate
  and and_4 (out_8, ~in_4, in_3, ~in_2, ~in_1);  // AND_Gate
  and and_5 (out_9, ~in_4, in_3, ~in_2, in_1);  // AND_Gate
  and and_6 (out_11, ~in_4, in_3, in_2, in_1);  // AND_Gate
  and and_7 (out_10, ~in_4, in_3, in_2, ~in_1);  // AND_Gate
  and and_8 (out_12, in_4, ~in_3, ~in_2, ~in_1);  // AND_Gate
  and and_9 (out_13, in_4, ~in_3, ~in_2, in_1);  // AND_Gate
  and and_10 (out_15, in_4, ~in_3, in_2, in_1);  // AND_Gate
  and and_11 (out_14, in_4, ~in_3, in_2, ~in_1);  // AND_Gate
  and and_12 (out_16, in_4, in_3, ~in_2, ~in_1);  // AND_Gate
  and and_13 (out_17, in_4, in_3, ~in_2, in_1);  // AND_Gate
  and and_14 (out_18, in_4, in_3, in_2, ~in_1);  // AND_Gate
  and and_15 (out_19, in_4, in_3, in_2, in_1);
endmodule

module extend (
  input  in_1,
  input  in_2,
  input  in_3,
  input  in_4,
  input  in_5,
  input  in_6,
  input  in_7,
  output [14:0] out_8,
  output [14:0] out_9,
  output [14:0] out_10,
  output [14:0] out_11,
  output [14:0] out_12,
  output [14:0] out_13,
  output [14:0] out_14
);

  assign out_8 = {{14{in_1}}, in_1};  // Bit_Extender bit_extender_1
  assign out_9 = {{14{in_2}}, in_2};  // Bit_Extender bit_extender_2
  assign out_10 = {{14{in_3}}, in_3};  // Bit_Extender bit_extender_3
  assign out_11 = {{14{in_4}}, in_4};  // Bit_Extender bit_extender_4
  assign out_12 = {{14{in_5}}, in_5};  // Bit_Extender bit_extender_5
  assign out_13 = {{14{in_6}}, in_6};  // Bit_Extender bit_extender_6
  assign out_14 = {{14{in_7}}, in_7};  // Bit_Extender bit_extender_7
endmodule

module extend2 (
  input  in_1,
  input  in_2,
  input  in_3,
  input  in_4,
  input  in_5,
  input  in_6,
  input  in_7,
  output [30:0] out_8,
  output [30:0] out_9,
  output [30:0] out_10,
  output [30:0] out_11,
  output [30:0] out_12,
  output [30:0] out_13,
  output [30:0] out_14
);

  assign out_8 = {{30{in_1}}, in_1};  // Bit_Extender bit_extender_1
  assign out_9 = {{30{in_2}}, in_2};  // Bit_Extender bit_extender_2
  assign out_10 = {{30{in_3}}, in_3};  // Bit_Extender bit_extender_3
  assign out_11 = {{30{in_4}}, in_4};  // Bit_Extender bit_extender_4
  assign out_12 = {{30{in_5}}, in_5};  // Bit_Extender bit_extender_5
  assign out_13 = {{30{in_6}}, in_6};  // Bit_Extender bit_extender_6
  assign out_14 = {{30{in_7}}, in_7};  // Bit_Extender bit_extender_7
endmodule
