// Logisim project Multiplier.circ as structural Verilog: 5 circuits, main circuit main
module main (
  input  in_1,
  input  in_2,
  input  in_3,
  input  in_4,
  input  in_5,
  input  in_6,
  input  in_7,
  input  in_8,
  input  in_9,
  input  in_10,
  input  in_11,
  input  in_12,
  input  in_13,
  input  in_14,
  input  in_15,
  input  in_16,
  input  B3,
  input  B2,
  input  B1,
  input  B0,
  input  A0,
  input  A1,
  input  A2,
  input  A3,
  input  A3_2,
  input  A2_2,
  input  A1_2,
  input  A0_2,
  input  B3_2,
  input  B2_2,
  input  B1_2,
  input  B0_2,
  input  B3_3,
  input  B2_3,
  input  B1_3,
  input  B0_3,
  input  A3_3,
  input  A2_3,
  input  A1_3,
  input  A0_3,
  output out_41,
  output out_42,
  output out_43,
  output out_44,
  output out_45,
  output out_46,
  output out_47,
  output out_48,
  output R0,
  output R1,
  output R2,
  output R3,
  output R4,
  output R5,
  output R6,
  output R7,
  output R7_2,
  output R6_2,
  output R5_2,
  output R3_2,
  output R2_2,
  output R1_2,
  output R0_2,
  output R7_3,
  output R6_3,
  output R5_3,
  output R3_3,
  output R2_3,
  output R1_3,
  output R0_3
);

  wire multiply_1_cout, multiply_2_5_cout, multiply_2_5_sout, multiply_2_6_cout, multiply_2_6_sout,
       multiply_2_7_cout, multiply_2_7_sout, multiply_2_8_cout, multiply_2_8_sout, multiply_2_9_cout,
       multiply_2_9_sout, multiply_2_10_cout, multiply_2_10_sout, multiply_2_11_cout, multiply_2_12_cout,
       multiply_2_13_cout, multiply_2_13_sout, multiply_2_14_cout, multiply_2_14_sout, multiply_2_15_cout,
       multiply_2_15_sout, multiply_2_16_cout, multiply_2_cout, multiply_2_sout, multiply_3_cout,
       multiply_4_cout, multiply_5_cout, multiply_5_sout, multiply_6_sout, multiply_7_cout, multiply_7_sout,
       multiply_8_sout, multiply_9_sout, multiply_10_cout, multiply_12_cout, multiply_12_sout,
       multiply_13_cout, multiply_14_cout, multiply_14_sout, multiply_15_cout, multiply_15_sout,
       multiply_16_cout, multiply_16_sout, multiply_17_cout, multiply_17_sout, multiply_18_cout,
       multiply_19_cout, multiply_19_sout, multiply_20_cout, multiply_21_cout, multiply_21_sout,
       multiply_22_cout, multiply_22_sout, multiply_23_cout, multiply_24_cout, multiply_25_cout,
       multiply_25_sout, multiply_26_cout, multiply_27_cout, multiply_29_cout, multiply_29_sout,
       multiply_30_cout, multiply_30_sout, multiply_31_cout, multiply_32_cout, multiply_33_cout,
       multiply_33_sout, multiply_39_cout, multiply_40_cout, multiply_41_cout, multiply_a_1_cout,
       multiply_a_1_out_8, multiply_a_1_s, multiply_a_2_cout, multiply_a_2_out_5, multiply_a_2_out_8,
       multiply_a_2_s, multiply_a_3_cout, multiply_a_3_out_5, multiply_a_3_out_8, multiply_a_3_s,
       multiply_a_4_cout, multiply_a_4_out_8, multiply_a_4_s, multiply_a_5_cout, multiply_a_5_out_5,
       multiply_a_5_out_8, multiply_a_5_s, multiply_a_6_cout, multiply_a_6_out_8, multiply_a_6_s,
       multiply_a_7_cout, multiply_a_7_out_5, multiply_a_7_out_8, multiply_a_7_s, multiply_a_8_cout,
       multiply_a_8_out_8, multiply_a_8_s, multiply_a_9_cout, multiply_a_9_out_5, multiply_a_9_out_8,
       multiply_a_9_s, multiply_a_10_cout, multiply_a_10_out_5, multiply_a_10_out_8, multiply_a_10_s,
       multiply_a_11_cout, multiply_a_11_out_5, multiply_a_11_out_8, multiply_a_11_s, multiply_a_12_cout,
       multiply_a_12_out_5, multiply_a_12_out_8, multiply_a_12_s, multiply_a_13_cout, multiply_a_13_out_5,
       multiply_a_13_out_8, multiply_a_14_cout, multiply_a_14_out_5, multiply_a_14_out_8, multiply_a_15_cout,
       multiply_a_15_out_5, multiply_a_15_out_8, multiply_a_16_cout, multiply_a_16_out_5,
       multiply_a_16_out_8, multiply_b_1_cout, multiply_b_3_cout, multiply_b_4_cout;

  Multiply multiply_1 (.A(in_9), .Cin(1'b0), .Cout(multiply_1_cout), .B(in_1), .Sin(1'b0), .Sout(out_41));
  Multiply multiply_2 (
    .A(in_9), .Cin(multiply_1_cout), .Cout(multiply_2_cout), .B(in_2), .Sin(1'b0), .Sout(multiply_2_sout));
  Multiply multiply_3 (.A(in_11), .Cin(1'b0), .Cout(multiply_3_cout), .B(in_2), .Sin(multiply_2_sout), .Sout(out_42));
  Multiply multiply_4 (.A(B0), .Cin(1'b0), .Cout(multiply_4_cout), .B(A0), .Sin(1'b0), .Sout(R0));
  Multiply multiply_5 (
    .A(in_9), .Cin(multiply_2_cout), .Cout(multiply_5_cout), .B(in_3), .Sin(1'b0), .Sout(multiply_5_sout));
  Multiply multiply_6 (.A(in_9), .Cin(multiply_5_cout), .B(in_4), .Sin(1'b0), .Sout(multiply_6_sout));  // open: Cout
  Multiply multiply_7 (
    .A(in_11), .Cin(multiply_3_cout), .Cout(multiply_7_cout), .B(in_3), .Sin(multiply_5_sout),
    .Sout(multiply_7_sout));
  Multiply multiply_8 (
    .A(in_11), .Cin(multiply_7_cout), .B(in_4), .Sin(multiply_6_sout), .Sout(multiply_8_sout));  // open: Cout
  Multiply multiply_9 (
    .A(in_13), .Cin(multiply_10_cout), .B(in_4), .Sin(multiply_8_sout), .Sout(multiply_9_sout));  // open: Cout
  Multiply multiply_10 (.A(in_13), .Cin(1'b0), .Cout(multiply_10_cout), .B(in_3), .Sin(multiply_7_sout), .Sout(out_43));
  Multiply multiply_11 (.A(in_15), .Cin(1'b0), .B(in_4), .Sin(multiply_9_sout), .Sout(out_44));  // open: Cout
  Multiply multiply_12 (
    .A(B0), .Cin(multiply_4_cout), .Cout(multiply_12_cout), .B(A1), .Sin(1'b0), .Sout(multiply_12_sout));
  Multiply multiply_13 (.A(B1), .Cin(1'b0), .Cout(multiply_13_cout), .B(A0), .Sin(multiply_12_sout), .Sout(R1));
  Multiply multiply_14 (
    .A(B0), .Cin(multiply_12_cout), .Cout(multiply_14_cout), .B(A2), .Sin(1'b0), .Sout(multiply_14_sout));
  Multiply multiply_15 (
    .A(B0), .Cin(multiply_14_cout), .Cout(multiply_15_cout), .B(A3), .Sin(1'b0), .Sout(multiply_15_sout));
  Multiply multiply_16 (
    .A(B1), .Cin(multiply_13_cout), .Cout(multiply_16_cout), .B(A1), .Sin(multiply_14_sout),
    .Sout(multiply_16_sout));
  Multiply multiply_17 (
    .A(B1), .Cin(multiply_16_cout), .Cout(multiply_17_cout), .B(A2), .Sin(multiply_15_sout),
    .Sout(multiply_17_sout));
  Multiply multiply_18 (.A(B2), .Cin(1'b0), .Cout(multiply_18_cout), .B(A0), .Sin(multiply_16_sout), .Sout(R2));
  Multiply multiply_19 (
    .A(B2), .Cin(multiply_18_cout), .Cout(multiply_19_cout), .B(A1), .Sin(multiply_17_sout),
    .Sout(multiply_19_sout));
  Multiply multiply_20 (.A(B3), .Cin(1'b0), .Cout(multiply_20_cout), .B(A0), .Sin(multiply_19_sout), .Sout(R3));
  Multiply multiply_21 (
    .A(B1), .Cin(multiply_17_cout), .Cout(multiply_21_cout), .B(A3), .Sin(multiply_15_cout),
    .Sout(multiply_21_sout));
  Multiply multiply_22 (
    .A(B2), .Cin(multiply_19_cout), .Cout(multiply_22_cout), .B(A2), .Sin(multiply_21_sout),
    .Sout(multiply_22_sout));
  Multiply multiply_23 (
    .A(B3), .Cin(multiply_20_cout), .Cout(multiply_23_cout), .B(A1), .Sin(multiply_22_sout), .Sout(R4));
  Multiply_A multiply_a_1 (
    .A(1'b0), .in_4(multiply_a_2_out_5), .S(multiply_a_1_s), .B(1'b0), .in_2(A3_3), .Cout(multiply_a_1_cout),
    .out_8(multiply_a_1_out_8));  // open: out_5
  Multiply_A multiply_a_2 (
    .A(1'b0), .out_5(multiply_a_2_out_5), .in_4(multiply_a_9_out_5), .S(multiply_a_2_s), .B(1'b0),
    .in_2(A2_3), .Cout(multiply_a_2_cout), .out_8(multiply_a_2_out_8));
  Multiply_A multiply_a_3 (
    .A(multiply_a_1_s), .out_5(multiply_a_3_out_5), .in_4(multiply_a_10_out_5), .S(multiply_a_3_s),
    .B(multiply_a_2_cout), .in_2(multiply_a_2_out_8), .Cout(multiply_a_3_cout), .out_8(multiply_a_3_out_8));
  Multiply_A multiply_a_4 (
    .A(1'b0), .in_4(multiply_a_3_out_5), .S(multiply_a_4_s), .B(multiply_a_1_cout),
    .in_2(multiply_a_1_out_8), .Cout(multiply_a_4_cout), .out_8(multiply_a_4_out_8));  // open: out_5
  Multiply_A multiply_a_5 (
    .A(multiply_a_4_s), .out_5(multiply_a_5_out_5), .in_4(multiply_a_11_out_5), .S(multiply_a_5_s),
    .B(multiply_a_3_cout), .in_2(multiply_a_3_out_8), .Cout(multiply_a_5_cout), .out_8(multiply_a_5_out_8));
  Multiply_A multiply_a_6 (
    .A(1'b0), .in_4(multiply_a_5_out_5), .S(multiply_a_6_s), .B(multiply_a_4_cout),
    .in_2(multiply_a_4_out_8), .Cout(multiply_a_6_cout), .out_8(multiply_a_6_out_8));  // open: out_5
  Multiply_A multiply_a_7 (
    .A(multiply_a_6_s), .out_5(multiply_a_7_out_5), .in_4(multiply_a_12_out_5), .S(multiply_a_7_s),
    .B(multiply_a_5_cout), .in_2(multiply_a_5_out_8), .Cout(multiply_a_7_cout), .out_8(multiply_a_7_out_8));
  Multiply_A multiply_a_8 (
    .A(1'b0), .in_4(multiply_a_7_out_5), .S(multiply_a_8_s), .B(multiply_a_6_cout),
    .in_2(multiply_a_6_out_8), .Cout(multiply_a_8_cout), .out_8(multiply_a_8_out_8));  // open: out_5
  Multiply_B multiply_b_1 (
    .A(multiply_a_8_s), .in_4(multiply_b_3_cout), .in_1(multiply_a_7_cout), .in_2(multiply_a_7_out_8),
    .Cout(multiply_b_1_cout), .S(R7_3));  // open: out_5
  Multiply_B multiply_b_2 (
    .A(1'b0), .in_4(multiply_b_1_cout), .in_1(multiply_a_8_cout), .in_2(multiply_a_8_out_8));  // open: out_5, Cout, S
  Multiply multiply_24 (.A(in_10), .Cin(1'b0), .Cout(multiply_24_cout), .B(in_5), .Sin(1'b0), .Sout(out_45));
  Multiply multiply_25 (
    .A(B2), .Cin(multiply_22_cout), .Cout(multiply_25_cout), .B(A3), .Sin(multiply_21_cout),
    .Sout(multiply_25_sout));
  Multiply multiply_26 (
    .A(B3), .Cin(multiply_23_cout), .Cout(multiply_26_cout), .B(A2), .Sin(multiply_25_sout), .Sout(R5));
  Multiply_A multiply_a_9 (
    .A(1'b0), .out_5(multiply_a_9_out_5), .in_4(multiply_a_13_out_5), .S(multiply_a_9_s), .B(1'b0),
    .in_2(A1_3), .Cout(multiply_a_9_cout), .out_8(multiply_a_9_out_8));
  Multiply_A multiply_a_10 (
    .A(multiply_a_2_s), .out_5(multiply_a_10_out_5), .in_4(multiply_a_14_out_5), .S(multiply_a_10_s),
    .B(multiply_a_9_cout), .in_2(multiply_a_9_out_8), .Cout(multiply_a_10_cout), .out_8(multiply_a_10_out_8));
  Multiply_A multiply_a_11 (
    .A(multiply_a_3_s), .out_5(multiply_a_11_out_5), .in_4(multiply_a_15_out_5), .S(multiply_a_11_s),
    .B(multiply_a_10_cout), .in_2(multiply_a_10_out_8), .Cout(multiply_a_11_cout), .out_8(multiply_a_11_out_8));
  Multiply_A multiply_a_12 (
    .A(multiply_a_5_s), .out_5(multiply_a_12_out_5), .in_4(multiply_a_16_out_5), .S(multiply_a_12_s),
    .B(multiply_a_11_cout), .in_2(multiply_a_11_out_8), .Cout(multiply_a_12_cout), .out_8(multiply_a_12_out_8));
  Multiply_B multiply_b_3 (
    .A(multiply_a_7_s), .in_4(multiply_b_4_cout), .in_1(multiply_a_12_cout), .in_2(multiply_a_12_out_8),
    .Cout(multiply_b_3_cout), .S(R6_3));  // open: out_5
  Multiply multiply_27 (
    .A(in_10), .Cin(multiply_24_cout), .Cout(multiply_27_cout), .B(in_6), .Sin(1'b0), .Sout(out_46));
  Multiply multiply_28 (.A(B3), .Cin(multiply_26_cout), .Cout(R7), .B(A3), .Sin(multiply_25_cout), .Sout(R6));
  Multiply_A multiply_a_13 (
    .A(1'b0), .out_5(multiply_a_13_out_5), .in_4(B0_3), .S(R0_3), .B(1'b0), .in_2(A0_3),
    .Cout(multiply_a_13_cout), .out_8(multiply_a_13_out_8));
  Multiply_A multiply_a_14 (
    .A(multiply_a_9_s), .out_5(multiply_a_14_out_5), .in_4(B1_3), .S(R1_3), .B(multiply_a_13_cout),
    .in_2(multiply_a_13_out_8), .Cout(multiply_a_14_cout), .out_8(multiply_a_14_out_8));
  Multiply_A multiply_a_15 (
    .A(multiply_a_10_s), .out_5(multiply_a_15_out_5), .in_4(B2_3), .S(R2_3), .B(multiply_a_14_cout),
    .in_2(multiply_a_14_out_8), .Cout(multiply_a_15_cout), .out_8(multiply_a_15_out_8));
  Multiply_A multiply_a_16 (
    .A(multiply_a_11_s), .out_5(multiply_a_16_out_5), .in_4(B3_3), .S(R3_3), .B(multiply_a_15_cout),
    .in_2(multiply_a_15_out_8), .Cout(multiply_a_16_cout), .out_8(multiply_a_16_out_8));
  Multiply_B multiply_b_4 (
    .A(multiply_a_12_s), .in_4(1'b0), .in_1(multiply_a_16_cout), .in_2(multiply_a_16_out_8),
    .Cout(multiply_b_4_cout), .S(R5_3));  // open: out_5
  Multiply multiply_29 (
    .A(in_10), .Cin(multiply_27_cout), .Cout(multiply_29_cout), .B(in_7), .Sin(1'b0), .Sout(multiply_29_sout));
  Multiply multiply_30 (
    .A(in_10), .Cin(multiply_29_cout), .Cout(multiply_30_cout), .B(in_8), .Sin(1'b0), .Sout(multiply_30_sout));
  Multiply multiply_31 (
    .A(in_12), .Cin(1'b0), .Cout(multiply_31_cout), .B(in_7), .Sin(multiply_29_sout), .Sout(out_47));
  Multiply multiply_32 (
    .A(in_12), .Cin(multiply_31_cout), .Cout(multiply_32_cout), .B(in_8), .Sin(multiply_30_sout),
    .Sout(out_48));
  Multiply multiply_33 (
    .A(in_12), .Cin(multiply_32_cout), .Cout(multiply_33_cout), .B(multiply_30_cout), .Sin(1'b0),
    .Sout(multiply_33_sout));
  Multiply multiply_34 (.A(in_14), .Cin(1'b0), .B(1'b0), .Sin(multiply_33_sout));  // open: Cout, Sout
  Multiply multiply_35 (.A(in_12), .Cin(multiply_33_cout), .B(1'b0), .Sin(1'b0));  // open: Cout, Sout
  Multiply multiply_36 (.A(in_14));  // open: Cin, Cout, B, Sin, Sout
  Multiply multiply_37 (.A(in_14));  // open: Cin, Cout, B, Sin, Sout
  Multiply multiply_38 (.A(in_14));  // open: Cin, Cout, B, Sin, Sout
  Multiply multiply_39 (.A(in_16), .Cin(1'b0), .Cout(multiply_39_cout));  // open: B, Sin, Sout
  Multiply multiply_40 (.A(in_16), .Cin(multiply_39_cout), .Cout(multiply_40_cout));  // open: B, Sin, Sout
  Multiply_2 multiply_2_1 (.Sin(1'b0), .Cin(multiply_2_5_cout), .A(B3_2), .B(A3_2), .Sout(R7_2));  // open: Cout
  Multiply_2 multiply_2_2 (
    .Sin(multiply_2_5_sout), .Cin(multiply_2_7_cout), .A(B2_2), .B(A3_2), .Sout(R6_2));  // open: Cout
  Multiply_2 multiply_2_3 (
    .Sin(multiply_2_7_sout), .Cin(multiply_2_9_cout), .A(B1_2), .B(A3_2), .Sout(R5_2));  // open: Cout
  Multiply_2 multiply_2_4 (
    .Sin(multiply_2_9_sout), .Cin(multiply_2_12_cout), .A(B0_2), .B(A3_2), .Sout(R3_2));  // open: Cout
  Multiply multiply_41 (.A(in_16), .Cin(multiply_40_cout), .Cout(multiply_41_cout));  // open: B, Sin, Sout
  Multiply_2 multiply_2_5 (
    .Cout(multiply_2_5_cout), .Sin(1'b0), .Cin(multiply_2_6_cout), .A(B3_2), .B(A2_2),
    .Sout(multiply_2_5_sout));
  Multiply_2 multiply_2_6 (
    .Cout(multiply_2_6_cout), .Sin(1'b0), .Cin(multiply_2_13_cout), .A(B3_2), .B(A1_2),
    .Sout(multiply_2_6_sout));
  Multiply_2 multiply_2_7 (
    .Cout(multiply_2_7_cout), .Sin(multiply_2_6_sout), .Cin(multiply_2_8_cout), .A(B2_2), .B(A2_2),
    .Sout(multiply_2_7_sout));
  Multiply_2 multiply_2_8 (
    .Cout(multiply_2_8_cout), .Sin(multiply_2_13_sout), .Cin(multiply_2_14_cout), .A(B2_2), .B(A1_2),
    .Sout(multiply_2_8_sout));
  Multiply_2 multiply_2_9 (
    .Cout(multiply_2_9_cout), .Sin(multiply_2_8_sout), .Cin(multiply_2_10_cout), .A(B1_2), .B(A2_2),
    .Sout(multiply_2_9_sout));
  Multiply_2 multiply_2_10 (
    .Cout(multiply_2_10_cout), .Sin(multiply_2_14_sout), .Cin(multiply_2_15_cout), .A(B1_2), .B(A1_2),
    .Sout(multiply_2_10_sout));
  Multiply_2 multiply_2_11 (
    .Cout(multiply_2_11_cout), .Sin(multiply_2_15_sout), .Cin(multiply_2_16_cout), .A(B0_2), .B(A1_2),
    .Sout(R1_2));
  Multiply_2 multiply_2_12 (
    .Cout(multiply_2_12_cout), .Sin(multiply_2_10_sout), .Cin(multiply_2_11_cout), .A(B0_2), .B(A2_2),
    .Sout(R2_2));
  Multiply multiply_42 (.A(in_16), .Cin(multiply_41_cout));  // open: Cout, B, Sin, Sout
  Multiply_2 multiply_2_13 (
    .Cout(multiply_2_13_cout), .Sin(1'b0), .Cin(1'b0), .A(B3_2), .B(A0_2), .Sout(multiply_2_13_sout));
  Multiply_2 multiply_2_14 (
    .Cout(multiply_2_14_cout), .Sin(1'b0), .Cin(1'b0), .A(B2_2), .B(A0_2), .Sout(multiply_2_14_sout));
  Multiply_2 multiply_2_15 (
    .Cout(multiply_2_15_cout), .Sin(1'b0), .Cin(1'b0), .A(B1_2), .B(A0_2), .Sout(multiply_2_15_sout));
  Multiply_2 multiply_2_16 (.Cout(multiply_2_16_cout), .Sin(1'b0), .Cin(1'b0), .A(B0_2), .B(A0_2), .Sout(R0_2));
endmodule

module Multiply (
  input  B,
  input  Sin,
  input  A,
  input  Cin,
  output Cout,
  output Sout
);

  wire and_1_out;

  and and_1 (and_1_out, A, B);
  Adder #(.width(1)) adder_1 (.a(and_1_out), .b(Sin), .out(Sout), .cin(Cin), .cout(Cout));
endmodule

module Multiply_2 (
  input  A,
  input  B,
  input  Sin,
  input  Cin,
  output Cout,
  output Sout
);

  wire and_1_out;

  and and_1 (and_1_out, B, A);
  Adder #(.width(1)) adder_1 (.a(and_1_out), .b(Sin), .out(Sout), .cin(Cin), .cout(Cout));
endmodule

module Multiply_A (
  input  B,
  input  in_2,
  input  A,
  input  in_4,
  output out_5,
  output S,
  output Cout,
  output out_8
);

  wire and_1_out;

  and and_1 (and_1_out, in_2, in_4);
  Adder #(.width(1)) adder_1 (.a(B), .b(A), .out(S), .cin(and_1_out), .cout(Cout));

  assign out_5 = in_4;
  assign out_8 = in_2;
endmodule

module Multiply_B (
  input  in_1,
  input  in_2,
  input  A,
  input  in_4,
  output out_5,
  output Cout,
  output S
);

  wire and_1_out;

  and and_1 (and_1_out, in_2, in_4);
  Adder #(.width(1)) adder_1 (.a(in_1), .b(A), .out(S), .cin(and_1_out), .cout(Cout));

  assign out_5 = in_4;
endmodule
