// Logisim project Programable.circ as structural Verilog
module Logic_Unit (
  input  in_1,
  input  [6:0] in_2,
  input  [6:0] in_3,
  input  [6:0] in_4,
  input  [6:0] in_5,
  input  [6:0] in_6,
  input  [6:0] in_7,
  input  in_8,
  input  [6:0] in_9,
  input  [6:0] in_10,
  input  [6:0] in_11,
  input  [6:0] in_12,
  input  [6:0] in_13,
  input  in_14,
  input  [6:0] in_15,
  input  [6:0] in_16,
  input  [7:0] in_17,
  input  in_18,
  input  in_19,
  input  in_20,
  input  in_21,
  input  in_22,
  input  in_23,
  input  in_24,
  input  in_25,
  input  in_26,
  output out_27,
  output out_28,
  output [7:0] out_29,
  output [6:0] out_30,
  output [6:0] out_31,
  output [6:0] out_32,
  output [6:0] out_33,
  output [6:0] out_34,
  output [6:0] out_35,
  output [6:0] out_36
);

  wire and_1_out, clock_1_out, equal_check_1_out_4, equal_check_1_out_5, shift_register_1_out, undriven,
       undriven_2, undriven_3;
  wire [6:0] long_switch_1_out_8, long_switch_1_out_9, long_switch_1_out_10, long_switch_1_out_11,
       long_switch_1_out_12, long_switch_1_out_13, sr_latch_1_out_3, sr_latch_2_out_3, switch_1_out_3,
       switch_2_out_3, switch_3_out_3, switch_4_out_3, switch_5_out_3, switch_6_out_3, switch_9_out_3,
       switch_10_out_3, switch_11_out_3, switch_12_out_3;

  // OR_Gate or_1 has open pins: in0=switch_1_out_3, in1=switch_6_out_3, out=open
  Long_Switch long_switch_1 (
    .in_6(in_2), .in_5(in_3), .in_4(in_4), .in_3(in_5), .in_2(in_6), .in_1(in_7),
    .out_13(long_switch_1_out_13), .out_12(long_switch_1_out_12), .out_11(long_switch_1_out_11),
    .out_10(long_switch_1_out_10), .out_9(long_switch_1_out_9), .out_8(long_switch_1_out_8));  // open: in_7
  Switch switch_1 (.in_1(long_switch_1_out_13), .out_3(switch_1_out_3), .in_2(undriven));
  Switch switch_2 (.in_1(in_15), .out_3(switch_2_out_3), .in_2(undriven));
  Switch switch_3 (.in_1(in_16), .out_3(switch_3_out_3));  // open: in_2
  SR_Latch sr_latch_1 (.in_1(switch_2_out_3), .out_3(sr_latch_1_out_3), .in_2(undriven_2));
  SR_Latch sr_latch_2 (.in_1(switch_3_out_3), .out_3(sr_latch_2_out_3), .in_2(undriven_2));
  Switch switch_4 (.in_1(sr_latch_2_out_3), .out_3(switch_4_out_3), .in_2(undriven_3));
  Switch switch_5 (.in_1(sr_latch_1_out_3), .out_3(switch_5_out_3), .in_2(undriven_3));
  Equal_Check equal_check_1 (
    .in_1(switch_5_out_3), .in_2(switch_4_out_3), .out_4(equal_check_1_out_4), .out_5(equal_check_1_out_5),
    .in_3(undriven_3));
  Switch switch_6 (.in_1(long_switch_1_out_12), .out_3(switch_6_out_3));  // open: in_2
  Switch switch_7 (.in_1(long_switch_1_out_11));  // open: out_3, in_2
  Switch switch_8 (.in_1(long_switch_1_out_10));  // open: out_3, in_2
  Switch switch_9 (.in_1(long_switch_1_out_9), .out_3(switch_9_out_3));  // open: in_2
  Switch switch_10 (.in_1(switch_9_out_3), .out_3(switch_10_out_3), .in_2(equal_check_1_out_4));
  assign out_35 = switch_10_out_3 | switch_12_out_3;  // OR_Gate or_2, 7 bits wide
  Switch switch_11 (.in_1(long_switch_1_out_8), .out_3(switch_11_out_3));  // open: in_2
  Switch switch_12 (.in_1(switch_11_out_3), .out_3(switch_12_out_3), .in_2(equal_check_1_out_5));
  and and_1 (and_1_out, ~in_18, in_19);  // AND_Gate
  Shift_Register shift_register_1 (
    .shift(and_1_out), .in(shift_register_1_out), .clk(clock_1_out), .out(shift_register_1_out),
    .load(in_18), .clr(in_23), .d0(in_17[7]), .q0(out_29[7]), .d1(in_17[6]), .q1(out_29[6]), .d2(in_17[5]),
    .q2(out_29[5]), .d3(in_17[4]), .q3(out_29[4]), .d4(in_17[3]), .q4(out_29[3]), .d5(in_17[2]),
    .q5(out_29[2]), .d6(in_17[1]), .q6(out_29[1]), .d7(in_17[0]), .q7(out_29[0]));
  Clock clock_1 (.out(clock_1_out));
  S_R_Flip_Flop s_r_ff_1 (
    .S(in_20), .clk(in_21), .R(in_22), .Q(out_27), .Qn(out_28), .preset(in_24), .reset(in_26), .en(in_25));
endmodule

module Switch (
  input  [6:0] in_1,
  input  in_2,
  output [6:0] out_3
);

  assign out_3 = in_1 & {7{in_2}};  // AND_Gate and_1, 7 bits wide
endmodule

module Long_Switch (
  input  [6:0] in_1,
  input  [6:0] in_2,
  input  [6:0] in_3,
  input  [6:0] in_4,
  input  [6:0] in_5,
  input  [6:0] in_6,
  input  in_7,
  output [6:0] out_8,
  output [6:0] out_9,
  output [6:0] out_10,
  output [6:0] out_11,
  output [6:0] out_12,
  output [6:0] out_13
);

  Switch switch_1 (.in_1(in_6), .out_3(out_13), .in_2(in_7));
  Switch switch_2 (.in_1(in_5), .out_3(out_12), .in_2(in_7));
  Switch switch_3 (.in_1(in_4), .out_3(out_11), .in_2(in_7));
  Switch switch_4 (.in_1(in_3), .out_3(out_10), .in_2(in_7));
  Switch switch_5 (.in_1(in_1), .out_3(out_8), .in_2(in_7));
  Switch switch_6 (.in_1(in_2), .out_3(out_9), .in_2(in_7));
endmodule

module SR_Latch (
  input  [6:0] in_1,
  input  in_2,
  output [6:0] out_3
);

  S_R_Flip_Flop s_r_ff_1 (.Q(out_3[6]), .preset(in_1[0]), .reset(in_2));  // open: S, clk, R, Qn, en
  S_R_Flip_Flop s_r_ff_2 (.Q(out_3[4]), .preset(in_1[2]), .reset(in_2));  // open: S, clk, R, Qn, en
  S_R_Flip_Flop s_r_ff_3 (.Q(out_3[5]), .preset(in_1[1]), .reset(in_2));  // open: S, clk, R, Qn, en
  S_R_Flip_Flop s_r_ff_4 (.Q(out_3[3]), .preset(in_1[3]), .reset(in_2));  // open: S, clk, R, Qn, en
  S_R_Flip_Flop s_r_ff_5 (.Q(out_3[2]), .preset(in_1[4]), .reset(in_2));  // open: S, clk, R, Qn, en
  S_R_Flip_Flop s_r_ff_6 (.Q(out_3[0]), .preset(in_1[6]), .reset(in_2));  // open: S, clk, R, Qn, en
  S_R_Flip_Flop s_r_ff_7 (.Q(out_3[1]), .preset(in_1[5]), .reset(in_2));  // open: S, clk, R, Qn, en
endmodule

module Equal_Check (
  input  [6:0] in_1,
  input  [6:0] in_2,
  input  in_3,
  output out_4,
  output out_5
);

  wire and_1_out, not_2_out;
  wire [6:0] not_1_out, xor_1_out;

  assign xor_1_out = in_1 ^ in_2;  // XOR_Gate xor_1, 7 bits wide
  assign not_1_out = ~xor_1_out;  // NOT_Gate not_1, 7 bits wide
  and and_1 (and_1_out, not_1_out[6], not_1_out[5], not_1_out[4], not_1_out[3], not_1_out[2], not_1_out[1], not_1_out[0]);
  and and_2 (out_4, and_1_out, in_3);
  not not_2 (not_2_out, and_1_out);
  and and_3 (out_5, not_2_out, in_3);
endmodule
