// Logisim project Regester.circ as structural Verilog: 6 circuits, main circuit main
module main (
  input  in_1,
  input  in_2,
  input  in_3,
  input  in_4,
  input  in_5,
  input  in_6,
  output out_7,
  output out_8,
  output out_9,
  output out_10
);

  Regester regester_1 (.in_1(in_1), .in_2(in_5), .in_3(in_6), .out_4(out_7));
  Regester regester_2 (.in_1(in_2), .in_2(in_5), .in_3(in_6), .out_4(out_8));
  Regester regester_3 (.in_1(in_3), .in_2(in_5), .in_3(in_6), .out_4(out_9));
  Regester regester_4 (.in_1(in_4), .in_2(in_5), .in_3(in_6), .out_4(out_10));
endmodule

module SR_Latch (
  input  in_1,
  input  in_2,
  output out_3
);

  wire nor_2_out;

  nor nor_1 (out_3, in_1, nor_2_out);
  nor nor_2 (nor_2_out, in_2, out_3);
endmodule

module D_Latch (
  input  in_1,
  input  in_2,
  output out_3
);

  wire and_1_out, and_2_out, not_1_out;

  not not_1 (not_1_out, in_1);
  and and_1 (and_1_out, not_1_out, in_2);
  and and_2 (and_2_out, in_1, in_2);
  SR_Latch sr_latch_1 (.in_1(and_1_out), .in_2(and_2_out), .out_3(out_3));
endmodule

module D_Flip_Flop (
  input  in_1,
  input  in_2,
  output out_3
);

  wire d_latch_2_out_3;

  D_Latch d_latch_1 (.in_1(d_latch_2_out_3), .in_2(in_2), .out_3(out_3));
  D_Latch d_latch_2 (.in_1(in_1), .in_2(in_2), .out_3(d_latch_2_out_3));
endmodule

module Regester (
  input  in_1,
  input  in_2,
  input  in_3,
  output out_4
);

  wire mux_1_out_4;

  MUX mux_1 (.in_1(out_4), .in_2(in_1), .in_3(in_2), .out_4(mux_1_out_4));
  D_Flip_Flop d_ff_1 (.in_1(mux_1_out_4), .in_2(in_3), .out_3(out_4));
endmodule

module MUX (
  input  in_1,
  input  in_2,
  input  in_3,
  output out_4
);

  wire and_1_out, and_2_out, not_1_out;

  not not_1 (not_1_out, in_3);
  and and_1 (and_1_out, in_1, not_1_out);
  and and_2 (and_2_out, in_2, in_3);
  or or_1 (out_4, and_1_out, and_2_out);
endmodule
