// Logisim project SUB.circ as structural Verilog: 3 circuits, main circuit main
module main (
  input  in_1,
  input  in_2,
  input  in_3,
  input  in_4,
  input  in_5,
  input  in_6,
  input  in_7,
  input  in_8,
  input  in_9,
  input  in_10,
  input  B,
  input  in_12,
  input  in_13,
  input  A_B_or_A_B,
  input  in_15,
  input  in_16,
  input  in_17,
  input  in_18,
  output out_19,
  output out_20,
  output out_21,
  output out_22,
  output out_23,
  output out_24,
  output out_25,
  output out_26,
  output out_27,
  output out_28
);

  wire add_1_out_4, add_2_out_4, add_3_out_4, add_4_out_4, sub_2_out_4, sub_3_out_4, sub_4_out_4, xor_1_out,
       xor_2_out, xor_3_out, xor_4_out;

  xor xor_1 (xor_1_out, in_10, B);
  sub sub_1 (.out_4(out_19), .in_1(in_1), .in_2(in_5), .out_5(out_20), .in_3(sub_2_out_4));
  xor xor_2 (xor_2_out, in_13, in_10);
  xor xor_3 (xor_3_out, in_10, in_12);
  sub sub_2 (.out_4(sub_2_out_4), .in_1(in_2), .in_2(in_6), .out_5(out_21), .in_3(sub_3_out_4));
  sub sub_3 (.out_4(sub_3_out_4), .in_1(in_3), .in_2(in_7), .out_5(out_22), .in_3(sub_4_out_4));
  xor xor_4 (xor_4_out, A_B_or_A_B, in_10);
  xor xor_5 (out_28, add_2_out_4, add_1_out_4);
  sub sub_4 (.out_4(sub_4_out_4), .in_1(in_4), .in_2(in_8), .out_5(out_23), .in_3(in_9));
  add add_1 (.out_4(add_1_out_4), .in_1(xor_1_out), .in_2(in_15), .out_5(out_24), .in_3(add_2_out_4));
  add add_2 (.out_4(add_2_out_4), .in_1(xor_3_out), .in_2(in_16), .out_5(out_25), .in_3(add_3_out_4));
  add add_3 (.out_4(add_3_out_4), .in_1(xor_2_out), .in_2(in_17), .out_5(out_26), .in_3(add_4_out_4));
  add add_4 (.out_4(add_4_out_4), .in_1(xor_4_out), .in_2(in_18), .out_5(out_27), .in_3(in_10));

  // Notes on the sheet:
  //   A
endmodule

module sub (
  input  in_1,
  input  in_2,
  input  in_3,
  output out_4,
  output out_5
);

  wire and_1_out, and_2_out, not_1_out, not_2_out, xor_1_out;

  or or_1 (out_4, and_1_out, and_2_out);
  not not_1 (not_1_out, in_2);
  and and_1 (and_1_out, not_1_out, in_1);
  not not_2 (not_2_out, xor_1_out);
  and and_2 (and_2_out, not_2_out, in_3);
  xor xor_1 (xor_1_out, in_1, in_2);
  xor xor_2 (out_5, in_3, xor_1_out);
endmodule

module add (
  input  in_1,
  input  in_2,
  input  in_3,
  output out_4,
  output out_5
);

  wire and_1_out, and_2_out, xor_1_out;

  or or_1 (out_4, and_1_out, and_2_out);
  and and_1 (and_1_out, in_2, in_1);
  and and_2 (and_2_out, xor_1_out, in_3);
  xor xor_1 (xor_1_out, in_1, in_2);
  xor xor_2 (out_5, in_3, xor_1_out);
endmodule
