// Logisim project Which-Is-Greater.circ as structural Verilog: 1 circuit, main circuit main
module main (
  input  in_1,
  input  in_2,
  input  in_3,
  input  in_4,
  input  in_5,
  input  in_6,
  input  in_7,
  input  in_8,
  input  in_9,
  input  in_10
);

  wire and_1_out, and_2_out, and_3_out, and_4_out, and_5_out, and_6_out, and_7_out, and_8_out, and_9_out,
       and_10_out, and_11_out, and_12_out, and_13_out, and_14_out, and_15_out, and_16_out, and_17_out,
       and_18_out, and_19_out, not_1_out, not_2_out, not_3_out, not_4_out, not_5_out, not_6_out, not_7_out,
       not_8_out, not_9_out, not_10_out, not_11_out, not_12_out, not_13_out, not_14_out, not_15_out,
       not_16_out, not_17_out, not_18_out, not_19_out, not_20_out, or_1_out, or_2_out, xnor_1_out,
       xnor_2_out, xnor_3_out, xnor_4_out, xnor_5_out;

  not not_1 (not_1_out, xnor_1_out);
  and and_1 (and_1_out, not_1_out, in_1, not_4_out);
  LED led_1 (.in(or_1_out));
  not not_2 (not_2_out, in_1);
  not not_3 (not_3_out, xnor_1_out);
  not not_4 (not_4_out, in_6);
  and and_2 (and_2_out, not_3_out, in_6, not_2_out);
  xnor xnor_1 (xnor_1_out, in_1, in_6);
  LED led_2 (.in(or_2_out));
  and and_3 (and_3_out, xnor_1_out, in_2);
  not not_5 (not_5_out, and_5_out);
  not not_6 (not_6_out, xnor_2_out);
  and and_4 (and_4_out, not_6_out, and_3_out, not_5_out);
  or or_1 (or_1_out, and_1_out, and_4_out, and_11_out, and_13_out, and_19_out);
  or or_2 (or_2_out, and_2_out, and_6_out, and_10_out, and_15_out, and_18_out);
  and and_5 (and_5_out, xnor_1_out, in_7);
  not not_7 (not_7_out, xnor_2_out);
  not not_8 (not_8_out, and_3_out);
  and and_6 (and_6_out, not_7_out, and_5_out, not_8_out);
  and and_7 (and_7_out, xnor_1_out, xnor_2_out, xnor_3_out, xnor_4_out, xnor_5_out);
  not not_9 (not_9_out, xnor_3_out);
  xnor xnor_2 (xnor_2_out, and_3_out, and_5_out);
  and and_8 (and_8_out, xnor_2_out, xnor_1_out, in_3);
  and and_9 (and_9_out, xnor_2_out, xnor_1_out, in_8);
  not not_10 (not_10_out, xnor_3_out);
  not not_11 (not_11_out, and_9_out);
  and and_10 (and_10_out, not_10_out, and_9_out, not_12_out);
  and and_11 (and_11_out, not_9_out, and_8_out, not_11_out);
  not not_12 (not_12_out, and_8_out);
  xnor xnor_3 (xnor_3_out, and_8_out, and_9_out);
  LED led_3 (.in(and_7_out));
  and and_12 (and_12_out, xnor_3_out, xnor_2_out, xnor_1_out, in_4);
  not not_13 (not_13_out, and_14_out);
  not not_14 (not_14_out, xnor_4_out);
  and and_13 (and_13_out, not_14_out, and_12_out, not_13_out);
  and and_14 (and_14_out, xnor_3_out, xnor_2_out, xnor_1_out, in_9);
  not not_15 (not_15_out, and_12_out);
  not not_16 (not_16_out, xnor_4_out);
  and and_15 (and_15_out, not_16_out, and_14_out, not_15_out);
  not not_17 (not_17_out, xnor_5_out);
  xnor xnor_4 (xnor_4_out, and_12_out, and_14_out);
  and and_16 (and_16_out, xnor_4_out, xnor_3_out, xnor_2_out, xnor_1_out, in_10);
  and and_17 (and_17_out, xnor_4_out, xnor_3_out, xnor_2_out, xnor_1_out, in_5);
  not not_18 (not_18_out, and_16_out);
  not not_19 (not_19_out, xnor_5_out);
  and and_18 (and_18_out, not_19_out, and_16_out, not_20_out);
  and and_19 (and_19_out, not_17_out, and_17_out, not_18_out);
  not not_20 (not_20_out, and_17_out);
  xnor xnor_5 (xnor_5_out, and_17_out, and_16_out);
endmodule
